// Logisim project project-3-main.circ as structural Verilog: 20 circuits, main circuit D_Latch
module D_Latch (
  input  Clock,
  input  D,
  input  Reset,
  output Q,
  output Qn
);

  wire and_1_out, and_2_out, and_3_out, and_4_out, and_5_out, and_6_out, not_1_out, not_2_out, not_3_out,
       not_4_out, not_5_out;

  not not_1 (not_1_out, Reset);
  and and_1 (and_1_out, not_5_out, not_3_out);
  and and_2 (and_2_out, not_2_out, Clock, not_1_out);
  and and_3 (and_3_out, not_3_out, Clock, not_5_out);
  and and_4 (and_4_out, not_4_out, D, not_1_out);
  not not_2 (not_2_out, and_1_out);
  not not_3 (not_3_out, and_2_out);
  not not_4 (not_4_out, and_3_out);
  not not_5 (not_5_out, and_4_out);
  and and_5 (and_5_out, not_3_out, Qn);
  not not_6 (Q, and_5_out);
  and and_6 (and_6_out, Q, not_4_out, not_1_out);
  not not_7 (Qn, and_6_out);
endmodule

module Sixteen_Bit_Register (
  input  D0,
  input  D1,
  input  D2,
  input  D3,
  input  Clock,
  input  Reset,
  input  D4,
  input  D5,
  input  D6,
  input  D7,
  input  D8,
  input  D9,
  input  D10,
  input  D11,
  input  D12,
  input  D13,
  input  D14,
  input  D15,
  output Q0,
  output Q1,
  output Q2,
  output Q3,
  output Q4,
  output Q5,
  output Q6,
  output Q7,
  output Q8,
  output Q9,
  output Q10,
  output Q11,
  output Q12,
  output Q13,
  output Q14,
  output Q15
);

  D_Latch d_latch_1 (.Q(Q0), .Clock(Clock), .D(D0), .Reset(Reset));  // open: Qn
  D_Latch d_latch_2 (.Q(Q4), .Clock(Clock), .D(D4), .Reset(Reset));  // open: Qn
  D_Latch d_latch_3 (.Q(Q8), .Clock(Clock), .D(D8), .Reset(Reset));  // open: Qn
  D_Latch d_latch_4 (.Q(Q12), .Clock(Clock), .D(D12), .Reset(Reset));  // open: Qn
  D_Latch d_latch_5 (.Q(Q1), .Clock(Clock), .D(D1), .Reset(Reset));  // open: Qn
  D_Latch d_latch_6 (.Q(Q5), .Clock(Clock), .D(D5), .Reset(Reset));  // open: Qn
  D_Latch d_latch_7 (.Q(Q9), .Clock(Clock), .D(D9), .Reset(Reset));  // open: Qn
  D_Latch d_latch_8 (.Q(Q13), .Clock(Clock), .D(D13), .Reset(Reset));  // open: Qn
  D_Latch d_latch_9 (.Q(Q2), .Clock(Clock), .D(D2), .Reset(Reset));  // open: Qn
  D_Latch d_latch_10 (.Q(Q6), .Clock(Clock), .D(D6), .Reset(Reset));  // open: Qn
  D_Latch d_latch_11 (.Q(Q10), .Clock(Clock), .D(D10), .Reset(Reset));  // open: Qn
  D_Latch d_latch_12 (.Q(Q14), .Clock(Clock), .D(D14), .Reset(Reset));  // open: Qn
  D_Latch d_latch_13 (.Q(Q3), .Clock(Clock), .D(D3), .Reset(Reset));  // open: Qn
  D_Latch d_latch_14 (.Q(Q7), .Clock(Clock), .D(D7), .Reset(Reset));  // open: Qn
  D_Latch d_latch_15 (.Q(Q11), .Clock(Clock), .D(D11), .Reset(Reset));  // open: Qn
  D_Latch d_latch_16 (.Q(Q15), .Clock(Clock), .D(D15), .Reset(Reset));  // open: Qn
endmodule

module Main (
);

  wire alu_1_z_out, Bus_In_CS, IR_S, IR_Shift_0_CS, mar_1_mar_mm_in, mdr_1_mdr_mm_out, r_o_m_1_rom_out,
       Reset, undriven, Y_Out_CS, y_register_1_s0, y_register_1_s1, y_register_1_s2, y_register_1_s3,
       y_register_1_y_out, z_register_1_psw_n, z_register_1_psw_z;
  wire [2:0] ir_1_ir_rd, ir_1_ir_rs1, ir_1_ir_rs2;
  wire [15:0] ir_1_op0;

  MM mm_1 (
    .MDR_in(undriven), .MAR_in(mar_1_mar_mm_in), .MDR_out(mdr_1_mdr_mm_out));  // open: WRITE_MM_CS, Clock, Reset, READ_MM_CS
  R_O_M r_o_m_1 (.ROM_Out(r_o_m_1_rom_out));  // open: Clock, Reset, ROM_Out_CS
  Timer timer_1 (.Timer_In(r_o_m_1_rom_out));  // open: Timer_Flag, Clock, Reset
  IR ir_1 (
    .IR_Rs1(ir_1_ir_rs1), .IR_Rs2(ir_1_ir_rs2), .IR_Rd(ir_1_ir_rd), .OP0(ir_1_op0[0]), .OP1(ir_1_op0[1]),
    .OP2(ir_1_op0[2]), .OP3(ir_1_op0[3]), .OP4(ir_1_op0[4]), .OP5(ir_1_op0[5]), .OP6(ir_1_op0[6]),
    .OP7(ir_1_op0[7]), .OP8(ir_1_op0[8]), .OP9(ir_1_op0[9]), .OP10(ir_1_op0[10]), .OP11(ir_1_op0[11]),
    .OP12(ir_1_op0[12]), .OP13(ir_1_op0[13]), .OP14(ir_1_op0[14]), .OP15(ir_1_op0[15]),
    .IR_In(r_o_m_1_rom_out));  // open: IR_Long_Offset, IR_Short_Offset, IR_S, IR_Shift, IR_OPcode, IR_In_CS, Clock, IR_Long_Off_CS, IR_Short_Off_CS, Reset
  MAR mar_1 (.MAR_MM_In(mar_1_mar_mm_in), .MAR_Bus_In(r_o_m_1_rom_out));  // open: MAR_Bus_In_CS, Clock, Reset
  MDR mdr_1 (
    .MDR_MM_Out(mdr_1_mdr_mm_out), .MDR_Bus_Out(r_o_m_1_rom_out), .MDR_MM_In(undriven),
    .MDR_Bus_In(r_o_m_1_rom_out));  // open: READ_MM, MDR_Bus_In_CS, Clock, Reset, MDR_Bus_Out_CS
  GPR gpr_1 (
    .GPR_0(r_o_m_1_rom_out), .GPR_1(r_o_m_1_rom_out), .GPR_2(r_o_m_1_rom_out), .GPR_3(r_o_m_1_rom_out),
    .GPR_4(r_o_m_1_rom_out), .GPR_5(r_o_m_1_rom_out), .GPR_6(r_o_m_1_rom_out), .GPR_7(r_o_m_1_rom_out),
    .IR_Rs2_In(ir_1_ir_rs2), .IR_Rd_In(ir_1_ir_rd), .IR_Rs1_In(ir_1_ir_rs1), .GPR_In_CS(r_o_m_1_rom_out));  // open: Clock, GPR_In, PC_In, Reset, GPR_0_Out_CS, PC_Out, GPR_Rd_In, GPR_Rd_Out, GPR_Rs1_In, GPR_Rs1_Out, GPR_Rs2_In, GPR_Rs_2_Out
  PSW psw_1 (
    .PSW_out(r_o_m_1_rom_out), .PSW_In(r_o_m_1_rom_out), .PSW_Z(z_register_1_psw_z),
    .PSW_N(z_register_1_psw_n));  // open: PSW_P, PSW_in_CS, Clock, Reset, PSW_out_CS
  Y_Register y_register_1 (
    .S0(y_register_1_s0), .S1(y_register_1_s1), .S2(y_register_1_s2), .S3(y_register_1_s3),
    .Y_Out(y_register_1_y_out), .Y_In(r_o_m_1_rom_out));  // open: Y_In_CS, Clock, Reset, Y_Out_CS
  ALU alu_1 (
    .Z_Out(alu_1_z_out), .Y_In(y_register_1_y_out), .S0(y_register_1_s3), .S1(y_register_1_s2),
    .S2(y_register_1_s1), .S3(y_register_1_s0), .OP0(ir_1_op0[0]), .OP1(ir_1_op0[1]), .OP2(ir_1_op0[2]),
    .OP3(ir_1_op0[3]), .OP4(ir_1_op0[4]), .OP5(ir_1_op0[5]), .Bus_In(r_o_m_1_rom_out));  // open: ALU_Inc_2, IR_Shift, IR_Shift_0_CS, ALU_Opcode_Task, Bus_In_CS, ALU_ADD, ALU_NOT
  Z_Register z_register_1 (
    .Z_Out(r_o_m_1_rom_out), .PSW_Z(z_register_1_psw_z), .PSW_N(z_register_1_psw_n), .Z_In(alu_1_z_out),
    .SET_CC(IR_S));  // open: Z_In_CS, Clock, Reset, Z_Out_CS
  Control_Unit control_unit_1 (
    .Reset(Reset), .ALU_In_Right(Bus_In_CS), .ALU_In_Left(Y_Out_CS), .ALU_Leftshift_IR_Shift(IR_Shift_0_CS),
    .Opcode(ir_1_op0));  // open: IR_In_CS, IR_Short_Off_CS, IR_Long_Off_CS, PC_In, PC_Out, GPR_Rd_In, GPR_Rd_Out, GPR_Rs2_Out, GPR_Rs1_Out, GPR_0_Out_CS, MAR_Bus_In_CS, MDR_Bus_Out_CS, MDR_Bus_In_CS, READ_MM, WRITE_MM, ALU_Opcode_Task, ALU_NOT, ALU_ADD, ALU_Inc_2, Z_In_CS, Z_Out_CS, Y_In_CS, ROM_Out_CS, Timer_In, PSW_In_CS, PSW_Out_CS, Clock, PSW_P, Timer_Flag, PSW_Z, PSW_N
endmodule

module R_O_M (
  input  Clock,
  input  Reset,
  input  ROM_Out_CS,
  output ROM_Out
);

  wire sixteen_bit_register_1_q0, sixteen_bit_register_1_q1, sixteen_bit_register_1_q2,
       sixteen_bit_register_1_q3, sixteen_bit_register_1_q4, sixteen_bit_register_1_q5,
       sixteen_bit_register_1_q6, sixteen_bit_register_1_q7, sixteen_bit_register_1_q8,
       sixteen_bit_register_1_q9, sixteen_bit_register_1_q10, sixteen_bit_register_1_q11,
       sixteen_bit_register_1_q12, sixteen_bit_register_1_q13, sixteen_bit_register_1_q14,
       sixteen_bit_register_1_q15;

  Sixteen_Bit_Register sixteen_bit_register_1 (
    .Q4(sixteen_bit_register_1_q4), .Q8(sixteen_bit_register_1_q8), .Q12(sixteen_bit_register_1_q12),
    .Q0(sixteen_bit_register_1_q0), .Q5(sixteen_bit_register_1_q5), .Q9(sixteen_bit_register_1_q9),
    .Q13(sixteen_bit_register_1_q13), .Q1(sixteen_bit_register_1_q1), .Q6(sixteen_bit_register_1_q6),
    .Q10(sixteen_bit_register_1_q10), .Q14(sixteen_bit_register_1_q14), .Q2(sixteen_bit_register_1_q2),
    .Q7(sixteen_bit_register_1_q7), .Q11(sixteen_bit_register_1_q11), .Q15(sixteen_bit_register_1_q15),
    .Q3(sixteen_bit_register_1_q3), .Clock(Clock), .Reset(Reset), .D0(1'b0), .D4(1'b0), .D8(1'b0),
    .D12(1'b0), .D1(1'b0), .D5(1'b0), .D9(1'b0), .D13(1'b0), .D2(1'b0), .D6(1'b0), .D10(1'b0), .D14(1'b0),
    .D3(1'b1), .D7(1'b0), .D11(1'b0), .D15(1'b0));
  assign ROM_Out = ROM_Out_CS ? sixteen_bit_register_1_q0 : 1'bz;  // Controlled_Buffer controlled_buffer_1
endmodule

module PSW (
  input  PSW_In,
  input  PSW_in_CS,
  input  PSW_Z,
  input  PSW_N,
  input  Clock,
  input  Reset,
  input  PSW_out_CS,
  output PSW_P,
  output PSW_out
);

  wire sixteen_bit_register_1_q0, sixteen_bit_register_1_q1, sixteen_bit_register_1_q3,
       sixteen_bit_register_1_q4, sixteen_bit_register_1_q5, sixteen_bit_register_1_q6,
       sixteen_bit_register_1_q7, sixteen_bit_register_1_q8, sixteen_bit_register_1_q9,
       sixteen_bit_register_1_q10, sixteen_bit_register_1_q11, sixteen_bit_register_1_q12,
       sixteen_bit_register_1_q13, sixteen_bit_register_1_q14, sixteen_bit_register_1_q15, undriven,
       undriven_2, undriven_3, undriven_4, undriven_5, undriven_6, undriven_7, undriven_8, undriven_9,
       undriven_10, undriven_11, undriven_12, undriven_13, undriven_14;

  assign PSW_N = PSW_in_CS ? PSW_In : 1'bz;  // Controlled_Buffer controlled_buffer_1
  Sixteen_Bit_Register sixteen_bit_register_1 (
    .Q4(sixteen_bit_register_1_q4), .Q8(sixteen_bit_register_1_q8), .Q12(sixteen_bit_register_1_q12),
    .Q0(sixteen_bit_register_1_q0), .Q5(sixteen_bit_register_1_q5), .Q9(sixteen_bit_register_1_q9),
    .Q13(sixteen_bit_register_1_q13), .Q1(sixteen_bit_register_1_q1), .Q6(sixteen_bit_register_1_q6),
    .Q10(sixteen_bit_register_1_q10), .Q14(sixteen_bit_register_1_q14), .Q2(PSW_P),
    .Q7(sixteen_bit_register_1_q7), .Q11(sixteen_bit_register_1_q11), .Q15(sixteen_bit_register_1_q15),
    .Q3(sixteen_bit_register_1_q3), .Clock(Clock), .Reset(Reset), .D0(PSW_N), .D4(undriven_12),
    .D8(undriven_8), .D12(undriven_4), .D1(PSW_Z), .D5(undriven_11), .D9(undriven_7), .D13(undriven_3),
    .D2(undriven_14), .D6(undriven_10), .D10(undriven_6), .D14(undriven_2), .D3(undriven_13),
    .D7(undriven_9), .D11(undriven_5), .D15(undriven));
  assign PSW_out = PSW_out_CS ? sixteen_bit_register_1_q0 : 1'bz;  // Controlled_Buffer controlled_buffer_2
endmodule

module IR (
  input  IR_In,
  input  IR_In_CS,
  input  Clock,
  input  Reset,
  input  IR_Long_Off_CS,
  input  IR_Short_Off_CS,
  output OP0,
  output OP1,
  output OP2,
  output [3:0] IR_OPcode,
  output OP3,
  output OP4,
  output OP5,
  output OP6,
  output OP7,
  output OP8,
  output OP9,
  output OP10,
  output [11:0] IR_Long_Offset,
  output OP11,
  output OP12,
  output [8:0] IR_Short_Offset,
  output OP13,
  output OP14,
  output IR_S,
  output OP15,
  output [1:0] IR_Shift,
  output [2:0] IR_Rd,
  output [2:0] IR_Rs1,
  output [2:0] IR_Rs2
);

  wire A_out, B_out, C_out, controlled_buffer_1_out, or_1_out, undriven, undriven_2, undriven_3, undriven_4,
       undriven_5, undriven_6, undriven_7, undriven_8, undriven_9, undriven_10, undriven_11, undriven_12,
       undriven_13, undriven_14, undriven_15;
  wire [11:0] sixteen_bit_register_1_q4;

  assign controlled_buffer_1_out = IR_In_CS ? IR_In : 1'bz;  // Controlled_Buffer controlled_buffer_1
  assign IR_Long_Offset = IR_Long_Off_CS ? sixteen_bit_register_1_q4 : 12'bz;  // Controlled_Buffer controlled_buffer_2
  assign IR_Short_Offset = IR_Short_Off_CS ? sixteen_bit_register_1_q4[11:3] : 9'bz;  // Controlled_Buffer controlled_buffer_3
  buf buffer_1 (IR_Long_Off_CS, C_out);
  buf buffer_2 (IR_Short_Off_CS, B_out);
  Sixteen_Bit_Register sixteen_bit_register_1 (
    .Q4(sixteen_bit_register_1_q4[0]), .Q8(sixteen_bit_register_1_q4[4]), .Q12(sixteen_bit_register_1_q4[8]),
    .Q0(IR_OPcode[0]), .Q5(sixteen_bit_register_1_q4[1]), .Q9(sixteen_bit_register_1_q4[5]),
    .Q13(sixteen_bit_register_1_q4[9]), .Q1(IR_OPcode[1]), .Q6(sixteen_bit_register_1_q4[2]),
    .Q10(sixteen_bit_register_1_q4[6]), .Q14(sixteen_bit_register_1_q4[10]), .Q2(IR_OPcode[2]),
    .Q7(sixteen_bit_register_1_q4[3]), .Q11(sixteen_bit_register_1_q4[7]),
    .Q15(sixteen_bit_register_1_q4[11]), .Q3(IR_OPcode[3]), .Clock(Clock), .Reset(Reset),
    .D0(controlled_buffer_1_out), .D4(undriven_12), .D8(undriven_8), .D12(undriven_4), .D1(undriven_15),
    .D5(undriven_11), .D9(undriven_7), .D13(undriven_3), .D2(undriven_14), .D6(undriven_10),
    .D10(undriven_6), .D14(undriven_2), .D3(undriven_13), .D7(undriven_9), .D11(undriven_5), .D15(undriven));
  assign IR_Rs1 = A_out ? sixteen_bit_register_1_q4[8:6] : 3'bz;  // Controlled_Buffer controlled_buffer_4
  assign IR_Rs2 = A_out ? sixteen_bit_register_1_q4[11:9] : 3'bz;  // Controlled_Buffer controlled_buffer_5
  Decoder #(.select(4)) decoder_1 (
    .out0(OP0), .out1(OP1), .out2(OP2), .out3(OP3), .out4(OP4), .out5(OP5), .out6(OP6), .out7(OP7),
    .out8(OP8), .out9(OP9), .out10(OP10), .out11(OP11), .out12(OP12), .out13(OP13), .out14(OP14),
    .out15(OP15), .sel(IR_OPcode));  // open: en
  assign IR_S = or_1_out ? sixteen_bit_register_1_q4[0] : 1'bz;  // Controlled_Buffer controlled_buffer_6
  or or_1 (or_1_out, A_out, B_out);
  assign IR_Shift = A_out ? sixteen_bit_register_1_q4[2:1] : 2'bz;  // Controlled_Buffer controlled_buffer_7
  assign IR_Rd = A_out ? sixteen_bit_register_1_q4[3:1] : 3'bz;  // Controlled_Buffer controlled_buffer_8
  assign IR_Rd = B_out ? sixteen_bit_register_1_q4[5:3] : 3'bz;  // Controlled_Buffer controlled_buffer_9
  or A (A_out, OP0, OP1, OP2, OP3, OP4, OP5);
  or B (B_out, OP6, OP7, OP8, OP12, OP13);
  or C (C_out, OP9, OP10, OP11, OP14, OP15);
endmodule

module Timer (
  input  Timer_In,
  input  Clock,
  input  Reset,
  output Timer_Flag
);

  wire sixteen_bit_register_1_q1, sixteen_bit_register_1_q2, sixteen_bit_register_1_q3,
       sixteen_bit_register_1_q4, sixteen_bit_register_1_q5, sixteen_bit_register_1_q6,
       sixteen_bit_register_1_q7, sixteen_bit_register_1_q8, sixteen_bit_register_1_q9,
       sixteen_bit_register_1_q10, sixteen_bit_register_1_q11, sixteen_bit_register_1_q12,
       sixteen_bit_register_1_q13, sixteen_bit_register_1_q14, sixteen_bit_register_1_q15, undriven,
       undriven_2, undriven_3, undriven_4, undriven_5, undriven_6, undriven_7, undriven_8, undriven_9,
       undriven_10, undriven_11, undriven_12, undriven_13, undriven_14, undriven_15;

  Sixteen_Bit_Register sixteen_bit_register_1 (
    .Q4(sixteen_bit_register_1_q4), .Q8(sixteen_bit_register_1_q8), .Q12(sixteen_bit_register_1_q12),
    .Q0(Timer_Flag), .Q5(sixteen_bit_register_1_q5), .Q9(sixteen_bit_register_1_q9),
    .Q13(sixteen_bit_register_1_q13), .Q1(sixteen_bit_register_1_q1), .Q6(sixteen_bit_register_1_q6),
    .Q10(sixteen_bit_register_1_q10), .Q14(sixteen_bit_register_1_q14), .Q2(sixteen_bit_register_1_q2),
    .Q7(sixteen_bit_register_1_q7), .Q11(sixteen_bit_register_1_q11), .Q15(sixteen_bit_register_1_q15),
    .Q3(sixteen_bit_register_1_q3), .Clock(Clock), .Reset(Reset), .D0(Timer_In), .D4(undriven_12),
    .D8(undriven_8), .D12(undriven_4), .D1(undriven_15), .D5(undriven_11), .D9(undriven_7), .D13(undriven_3),
    .D2(undriven_14), .D6(undriven_10), .D10(undriven_6), .D14(undriven_2), .D3(undriven_13),
    .D7(undriven_9), .D11(undriven_5), .D15(undriven));
endmodule

module GPR (
  input  Reset,
  input  GPR_In_CS,
  input  GPR_In,
  input  Clock,
  input  GPR_0_Out_CS,
  input  GPR_Rd_In,
  input  [2:0] IR_Rd_In,
  input  GPR_Rd_Out,
  input  [2:0] IR_Rs1_In,
  input  GPR_Rs1_In,
  input  GPR_Rs1_Out,
  input  [2:0] IR_Rs2_In,
  input  GPR_Rs2_In,
  input  GPR_Rs_2_Out,
  input  PC_In,
  input  PC_Out,
  output GPR_0,
  output GPR_1,
  output GPR_2,
  output GPR_3,
  output GPR_4,
  output GPR_5,
  output GPR_6,
  output GPR_7
);

  wire and_1_out, and_2_out, and_3_out, and_4_out, and_5_out, and_6_out, and_7_out, controlled_buffer_1_out,
       or_1_out, or_2_out, or_3_out, or_4_out, or_6_out, sixteen_bit_register_1_q0,
       sixteen_bit_register_1_q1, sixteen_bit_register_1_q2, sixteen_bit_register_1_q3,
       sixteen_bit_register_1_q4, sixteen_bit_register_1_q5, sixteen_bit_register_1_q6,
       sixteen_bit_register_1_q7, sixteen_bit_register_1_q8, sixteen_bit_register_1_q9,
       sixteen_bit_register_1_q10, sixteen_bit_register_1_q11, sixteen_bit_register_1_q12,
       sixteen_bit_register_1_q13, sixteen_bit_register_1_q14, sixteen_bit_register_1_q15,
       sixteen_bit_register_2_q0, sixteen_bit_register_2_q1, sixteen_bit_register_2_q2,
       sixteen_bit_register_2_q3, sixteen_bit_register_2_q4, sixteen_bit_register_2_q5,
       sixteen_bit_register_2_q6, sixteen_bit_register_2_q7, sixteen_bit_register_2_q8,
       sixteen_bit_register_2_q9, sixteen_bit_register_2_q10, sixteen_bit_register_2_q11,
       sixteen_bit_register_2_q12, sixteen_bit_register_2_q13, sixteen_bit_register_2_q14,
       sixteen_bit_register_2_q15, sixteen_bit_register_3_q0, sixteen_bit_register_3_q1,
       sixteen_bit_register_3_q2, sixteen_bit_register_3_q3, sixteen_bit_register_3_q4,
       sixteen_bit_register_3_q5, sixteen_bit_register_3_q6, sixteen_bit_register_3_q7,
       sixteen_bit_register_3_q8, sixteen_bit_register_3_q9, sixteen_bit_register_3_q10,
       sixteen_bit_register_3_q11, sixteen_bit_register_3_q12, sixteen_bit_register_3_q13,
       sixteen_bit_register_3_q14, sixteen_bit_register_3_q15, sixteen_bit_register_4_q0,
       sixteen_bit_register_4_q1, sixteen_bit_register_4_q2, sixteen_bit_register_4_q3,
       sixteen_bit_register_4_q4, sixteen_bit_register_4_q5, sixteen_bit_register_4_q6,
       sixteen_bit_register_4_q7, sixteen_bit_register_4_q8, sixteen_bit_register_4_q9,
       sixteen_bit_register_4_q10, sixteen_bit_register_4_q11, sixteen_bit_register_4_q12,
       sixteen_bit_register_4_q13, sixteen_bit_register_4_q14, sixteen_bit_register_4_q15,
       sixteen_bit_register_5_q0, sixteen_bit_register_5_q1, sixteen_bit_register_5_q2,
       sixteen_bit_register_5_q3, sixteen_bit_register_5_q4, sixteen_bit_register_5_q5,
       sixteen_bit_register_5_q6, sixteen_bit_register_5_q7, sixteen_bit_register_5_q8,
       sixteen_bit_register_5_q9, sixteen_bit_register_5_q10, sixteen_bit_register_5_q11,
       sixteen_bit_register_5_q12, sixteen_bit_register_5_q13, sixteen_bit_register_5_q14,
       sixteen_bit_register_5_q15, sixteen_bit_register_6_q0, sixteen_bit_register_6_q1,
       sixteen_bit_register_6_q2, sixteen_bit_register_6_q3, sixteen_bit_register_6_q4,
       sixteen_bit_register_6_q5, sixteen_bit_register_6_q6, sixteen_bit_register_6_q7,
       sixteen_bit_register_6_q8, sixteen_bit_register_6_q9, sixteen_bit_register_6_q10,
       sixteen_bit_register_6_q11, sixteen_bit_register_6_q12, sixteen_bit_register_6_q13,
       sixteen_bit_register_6_q14, sixteen_bit_register_6_q15, sixteen_bit_register_7_q0,
       sixteen_bit_register_7_q1, sixteen_bit_register_7_q2, sixteen_bit_register_7_q3,
       sixteen_bit_register_7_q4, sixteen_bit_register_7_q5, sixteen_bit_register_7_q6,
       sixteen_bit_register_7_q7, sixteen_bit_register_7_q8, sixteen_bit_register_7_q9,
       sixteen_bit_register_7_q10, sixteen_bit_register_7_q11, sixteen_bit_register_7_q12,
       sixteen_bit_register_7_q13, sixteen_bit_register_7_q14, sixteen_bit_register_7_q15,
       sixteen_bit_register_8_q0, sixteen_bit_register_8_q1, sixteen_bit_register_8_q2,
       sixteen_bit_register_8_q3, sixteen_bit_register_8_q4, sixteen_bit_register_8_q5,
       sixteen_bit_register_8_q6, sixteen_bit_register_8_q7, sixteen_bit_register_8_q8,
       sixteen_bit_register_8_q9, sixteen_bit_register_8_q10, sixteen_bit_register_8_q11,
       sixteen_bit_register_8_q12, sixteen_bit_register_8_q13, sixteen_bit_register_8_q14,
       sixteen_bit_register_8_q15, undriven, undriven_2, undriven_3, undriven_4, undriven_5, undriven_6,
       undriven_7, undriven_8, undriven_9, undriven_10, undriven_11, undriven_12, undriven_13, undriven_14,
       undriven_15, undriven_16, undriven_17, undriven_18, undriven_19, undriven_20, undriven_21,
       undriven_22, undriven_23, undriven_24, undriven_25, undriven_26, undriven_27, undriven_28,
       undriven_29, undriven_30, undriven_31, undriven_32, undriven_33, undriven_34, undriven_35,
       undriven_36, undriven_37, undriven_38, undriven_39, undriven_40, undriven_41, undriven_42,
       undriven_43, undriven_44, undriven_45, undriven_46, undriven_47, undriven_48, undriven_49,
       undriven_50, undriven_51, undriven_52, undriven_53, undriven_54, undriven_55, undriven_56,
       undriven_57, undriven_58, undriven_59, undriven_60, undriven_61, undriven_62, undriven_63,
       undriven_64, undriven_65, undriven_66, undriven_67, undriven_68, undriven_69, undriven_70,
       undriven_71, undriven_72, undriven_73, undriven_74, undriven_75, undriven_76, undriven_77,
       undriven_78, undriven_79, undriven_80, undriven_81, undriven_82, undriven_83, undriven_84,
       undriven_85, undriven_86, undriven_87, undriven_88, undriven_89, undriven_90, undriven_91,
       undriven_92, undriven_93, undriven_94, undriven_95, undriven_96, undriven_97, undriven_98,
       undriven_99, undriven_100, undriven_101, undriven_102, undriven_103, undriven_104, undriven_105;
  wire [6:1] buffer_1_out;
  wire [7:0] Dec_out, Decd_out, decoder_1_out0, decoder_2_out0, decoder_3_out0;
  wire [7:7] or_5_out;

  or or_1 (or_1_out, GPR_Rd_In, GPR_Rs1_In, GPR_Rs2_In);
  or or_2 (or_2_out, GPR_Rd_In, GPR_Rd_Out);
  or or_3 (or_3_out, GPR_Rs1_In, GPR_Rs1_Out);
  or or_4 (or_4_out, GPR_Rs2_In, GPR_Rs_2_Out);
  or or_5 (or_5_out[7], GPR_Rs_2_Out, GPR_Rs1_Out, GPR_Rd_Out);
  Decoder #(.select(3)) decoder_1 (
    .out0(decoder_1_out0[0]), .out1(decoder_1_out0[1]), .out2(decoder_1_out0[2]), .out3(decoder_1_out0[3]),
    .out4(decoder_1_out0[4]), .out5(decoder_1_out0[5]), .out6(decoder_1_out0[6]), .out7(decoder_1_out0[7]),
    .sel(IR_Rs2_In), .en(or_4_out));
  Decoder #(.select(3)) decoder_2 (
    .out0(decoder_2_out0[0]), .out1(decoder_2_out0[1]), .out2(decoder_2_out0[2]), .out3(decoder_2_out0[3]),
    .out4(decoder_2_out0[4]), .out5(decoder_2_out0[5]), .out6(decoder_2_out0[6]), .out7(decoder_2_out0[7]),
    .sel(IR_Rs1_In), .en(or_3_out));
  Decoder #(.select(3)) decoder_3 (
    .out0(decoder_3_out0[0]), .out1(decoder_3_out0[1]), .out2(decoder_3_out0[2]), .out3(decoder_3_out0[3]),
    .out4(decoder_3_out0[4]), .out5(decoder_3_out0[5]), .out6(decoder_3_out0[6]), .out7(decoder_3_out0[7]),
    .sel(IR_Rd_In), .en(or_2_out));
  assign Dec_out = decoder_3_out0 | decoder_2_out0 | decoder_1_out0;  // OR_Gate Dec, 8 bits wide
  assign controlled_buffer_1_out = GPR_In_CS ? GPR_In : 1'bz;  // Controlled_Buffer controlled_buffer_1
  and and_1 (and_1_out, Clock, or_1_out, Dec_out[1]);
  and and_2 (and_2_out, Clock, or_1_out, Dec_out[2]);
  and and_3 (and_3_out, Clock, or_1_out, Dec_out[3]);
  and and_4 (and_4_out, Clock, or_1_out, Dec_out[4]);
  and and_5 (and_5_out, Clock, or_1_out, Dec_out[5]);
  and and_6 (and_6_out, Clock, or_1_out, Dec_out[6]);
  and and_7 (and_7_out, Clock, or_1_out, Dec_out[7]);
  or or_6 (or_6_out, and_7_out, PC_In);
  assign Decd_out = Dec_out & {8{or_5_out[7]}};  // AND_Gate Decd, 8 bits wide
  Sixteen_Bit_Register sixteen_bit_register_1 (
    .Q4(sixteen_bit_register_1_q4), .Q8(sixteen_bit_register_1_q8), .Q12(sixteen_bit_register_1_q12),
    .Q0(sixteen_bit_register_1_q0), .Q5(sixteen_bit_register_1_q5), .Q9(sixteen_bit_register_1_q9),
    .Q13(sixteen_bit_register_1_q13), .Q1(sixteen_bit_register_1_q1), .Q6(sixteen_bit_register_1_q6),
    .Q10(sixteen_bit_register_1_q10), .Q14(sixteen_bit_register_1_q14), .Q2(sixteen_bit_register_1_q2),
    .Q7(sixteen_bit_register_1_q7), .Q11(sixteen_bit_register_1_q11), .Q15(sixteen_bit_register_1_q15),
    .Q3(sixteen_bit_register_1_q3), .Clock(Clock), .Reset(Reset), .D0(1'b0), .D4(1'b0), .D8(1'b0),
    .D12(1'b0), .D1(1'b0), .D5(1'b0), .D9(1'b0), .D13(1'b0), .D2(1'b0), .D6(1'b0), .D10(1'b0), .D14(1'b0),
    .D3(1'b0), .D7(1'b0), .D11(1'b0), .D15(1'b0));
  Sixteen_Bit_Register sixteen_bit_register_2 (
    .Q4(sixteen_bit_register_2_q4), .Q8(sixteen_bit_register_2_q8), .Q12(sixteen_bit_register_2_q12),
    .Q0(sixteen_bit_register_2_q0), .Q5(sixteen_bit_register_2_q5), .Q9(sixteen_bit_register_2_q9),
    .Q13(sixteen_bit_register_2_q13), .Q1(sixteen_bit_register_2_q1), .Q6(sixteen_bit_register_2_q6),
    .Q10(sixteen_bit_register_2_q10), .Q14(sixteen_bit_register_2_q14), .Q2(sixteen_bit_register_2_q2),
    .Q7(sixteen_bit_register_2_q7), .Q11(sixteen_bit_register_2_q11), .Q15(sixteen_bit_register_2_q15),
    .Q3(sixteen_bit_register_2_q3), .Clock(and_1_out), .Reset(Reset), .D0(controlled_buffer_1_out),
    .D4(undriven_78), .D8(undriven_50), .D12(undriven_22), .D1(undriven_99), .D5(undriven_71),
    .D9(undriven_43), .D13(undriven_15), .D2(undriven_92), .D6(undriven_64), .D10(undriven_36),
    .D14(undriven_8), .D3(undriven_85), .D7(undriven_57), .D11(undriven_29), .D15(undriven));
  Sixteen_Bit_Register sixteen_bit_register_3 (
    .Q4(sixteen_bit_register_3_q4), .Q8(sixteen_bit_register_3_q8), .Q12(sixteen_bit_register_3_q12),
    .Q0(sixteen_bit_register_3_q0), .Q5(sixteen_bit_register_3_q5), .Q9(sixteen_bit_register_3_q9),
    .Q13(sixteen_bit_register_3_q13), .Q1(sixteen_bit_register_3_q1), .Q6(sixteen_bit_register_3_q6),
    .Q10(sixteen_bit_register_3_q10), .Q14(sixteen_bit_register_3_q14), .Q2(sixteen_bit_register_3_q2),
    .Q7(sixteen_bit_register_3_q7), .Q11(sixteen_bit_register_3_q11), .Q15(sixteen_bit_register_3_q15),
    .Q3(sixteen_bit_register_3_q3), .Clock(and_2_out), .Reset(Reset), .D0(controlled_buffer_1_out),
    .D4(undriven_79), .D8(undriven_51), .D12(undriven_23), .D1(undriven_100), .D5(undriven_72),
    .D9(undriven_44), .D13(undriven_16), .D2(undriven_93), .D6(undriven_65), .D10(undriven_37),
    .D14(undriven_9), .D3(undriven_86), .D7(undriven_58), .D11(undriven_30), .D15(undriven_2));
  Sixteen_Bit_Register sixteen_bit_register_4 (
    .Q4(sixteen_bit_register_4_q4), .Q8(sixteen_bit_register_4_q8), .Q12(sixteen_bit_register_4_q12),
    .Q0(sixteen_bit_register_4_q0), .Q5(sixteen_bit_register_4_q5), .Q9(sixteen_bit_register_4_q9),
    .Q13(sixteen_bit_register_4_q13), .Q1(sixteen_bit_register_4_q1), .Q6(sixteen_bit_register_4_q6),
    .Q10(sixteen_bit_register_4_q10), .Q14(sixteen_bit_register_4_q14), .Q2(sixteen_bit_register_4_q2),
    .Q7(sixteen_bit_register_4_q7), .Q11(sixteen_bit_register_4_q11), .Q15(sixteen_bit_register_4_q15),
    .Q3(sixteen_bit_register_4_q3), .Clock(and_3_out), .Reset(Reset), .D0(controlled_buffer_1_out),
    .D4(undriven_80), .D8(undriven_52), .D12(undriven_24), .D1(undriven_101), .D5(undriven_73),
    .D9(undriven_45), .D13(undriven_17), .D2(undriven_94), .D6(undriven_66), .D10(undriven_38),
    .D14(undriven_10), .D3(undriven_87), .D7(undriven_59), .D11(undriven_31), .D15(undriven_3));
  Sixteen_Bit_Register sixteen_bit_register_5 (
    .Q4(sixteen_bit_register_5_q4), .Q8(sixteen_bit_register_5_q8), .Q12(sixteen_bit_register_5_q12),
    .Q0(sixteen_bit_register_5_q0), .Q5(sixteen_bit_register_5_q5), .Q9(sixteen_bit_register_5_q9),
    .Q13(sixteen_bit_register_5_q13), .Q1(sixteen_bit_register_5_q1), .Q6(sixteen_bit_register_5_q6),
    .Q10(sixteen_bit_register_5_q10), .Q14(sixteen_bit_register_5_q14), .Q2(sixteen_bit_register_5_q2),
    .Q7(sixteen_bit_register_5_q7), .Q11(sixteen_bit_register_5_q11), .Q15(sixteen_bit_register_5_q15),
    .Q3(sixteen_bit_register_5_q3), .Clock(and_4_out), .Reset(Reset), .D0(controlled_buffer_1_out),
    .D4(undriven_81), .D8(undriven_53), .D12(undriven_25), .D1(undriven_102), .D5(undriven_74),
    .D9(undriven_46), .D13(undriven_18), .D2(undriven_95), .D6(undriven_67), .D10(undriven_39),
    .D14(undriven_11), .D3(undriven_88), .D7(undriven_60), .D11(undriven_32), .D15(undriven_4));
  Sixteen_Bit_Register sixteen_bit_register_6 (
    .Q4(sixteen_bit_register_6_q4), .Q8(sixteen_bit_register_6_q8), .Q12(sixteen_bit_register_6_q12),
    .Q0(sixteen_bit_register_6_q0), .Q5(sixteen_bit_register_6_q5), .Q9(sixteen_bit_register_6_q9),
    .Q13(sixteen_bit_register_6_q13), .Q1(sixteen_bit_register_6_q1), .Q6(sixteen_bit_register_6_q6),
    .Q10(sixteen_bit_register_6_q10), .Q14(sixteen_bit_register_6_q14), .Q2(sixteen_bit_register_6_q2),
    .Q7(sixteen_bit_register_6_q7), .Q11(sixteen_bit_register_6_q11), .Q15(sixteen_bit_register_6_q15),
    .Q3(sixteen_bit_register_6_q3), .Clock(and_5_out), .Reset(Reset), .D0(controlled_buffer_1_out),
    .D4(undriven_82), .D8(undriven_54), .D12(undriven_26), .D1(undriven_103), .D5(undriven_75),
    .D9(undriven_47), .D13(undriven_19), .D2(undriven_96), .D6(undriven_68), .D10(undriven_40),
    .D14(undriven_12), .D3(undriven_89), .D7(undriven_61), .D11(undriven_33), .D15(undriven_5));
  Sixteen_Bit_Register sixteen_bit_register_7 (
    .Q4(sixteen_bit_register_7_q4), .Q8(sixteen_bit_register_7_q8), .Q12(sixteen_bit_register_7_q12),
    .Q0(sixteen_bit_register_7_q0), .Q5(sixteen_bit_register_7_q5), .Q9(sixteen_bit_register_7_q9),
    .Q13(sixteen_bit_register_7_q13), .Q1(sixteen_bit_register_7_q1), .Q6(sixteen_bit_register_7_q6),
    .Q10(sixteen_bit_register_7_q10), .Q14(sixteen_bit_register_7_q14), .Q2(sixteen_bit_register_7_q2),
    .Q7(sixteen_bit_register_7_q7), .Q11(sixteen_bit_register_7_q11), .Q15(sixteen_bit_register_7_q15),
    .Q3(sixteen_bit_register_7_q3), .Clock(and_6_out), .Reset(Reset), .D0(controlled_buffer_1_out),
    .D4(undriven_83), .D8(undriven_55), .D12(undriven_27), .D1(undriven_104), .D5(undriven_76),
    .D9(undriven_48), .D13(undriven_20), .D2(undriven_97), .D6(undriven_69), .D10(undriven_41),
    .D14(undriven_13), .D3(undriven_90), .D7(undriven_62), .D11(undriven_34), .D15(undriven_6));
  Sixteen_Bit_Register sixteen_bit_register_8 (
    .Q4(sixteen_bit_register_8_q4), .Q8(sixteen_bit_register_8_q8), .Q12(sixteen_bit_register_8_q12),
    .Q0(sixteen_bit_register_8_q0), .Q5(sixteen_bit_register_8_q5), .Q9(sixteen_bit_register_8_q9),
    .Q13(sixteen_bit_register_8_q13), .Q1(sixteen_bit_register_8_q1), .Q6(sixteen_bit_register_8_q6),
    .Q10(sixteen_bit_register_8_q10), .Q14(sixteen_bit_register_8_q14), .Q2(sixteen_bit_register_8_q2),
    .Q7(sixteen_bit_register_8_q7), .Q11(sixteen_bit_register_8_q11), .Q15(sixteen_bit_register_8_q15),
    .Q3(sixteen_bit_register_8_q3), .Clock(or_6_out), .Reset(Reset), .D0(controlled_buffer_1_out),
    .D4(undriven_84), .D8(undriven_56), .D12(undriven_28), .D1(undriven_105), .D5(undriven_77),
    .D9(undriven_49), .D13(undriven_21), .D2(undriven_98), .D6(undriven_70), .D10(undriven_42),
    .D14(undriven_14), .D3(undriven_91), .D7(undriven_63), .D11(undriven_35), .D15(undriven_7));
  assign {PC_Out, buffer_1_out, GPR_0_Out_CS} = Decd_out;  // Buffer buffer_1, 8 bits wide
  assign GPR_0 = GPR_0_Out_CS ? sixteen_bit_register_1_q0 : 1'bz;  // Controlled_Buffer controlled_buffer_2
  assign GPR_1 = buffer_1_out[1] ? sixteen_bit_register_2_q0 : 1'bz;  // Controlled_Buffer controlled_buffer_3
  assign GPR_2 = buffer_1_out[2] ? sixteen_bit_register_3_q0 : 1'bz;  // Controlled_Buffer controlled_buffer_4
  assign GPR_3 = buffer_1_out[3] ? sixteen_bit_register_4_q0 : 1'bz;  // Controlled_Buffer controlled_buffer_5
  assign GPR_4 = buffer_1_out[4] ? sixteen_bit_register_5_q0 : 1'bz;  // Controlled_Buffer controlled_buffer_6
  assign GPR_5 = buffer_1_out[5] ? sixteen_bit_register_6_q0 : 1'bz;  // Controlled_Buffer controlled_buffer_7
  assign GPR_6 = buffer_1_out[6] ? sixteen_bit_register_7_q0 : 1'bz;  // Controlled_Buffer controlled_buffer_8
  assign GPR_7 = PC_Out ? sixteen_bit_register_8_q0 : 1'bz;  // Controlled_Buffer controlled_buffer_9
endmodule

module MAR (
  input  MAR_Bus_In,
  input  MAR_Bus_In_CS,
  input  Clock,
  input  Reset,
  output MAR_MM_In
);

  wire controlled_buffer_1_out, sixteen_bit_register_1_q1, sixteen_bit_register_1_q2,
       sixteen_bit_register_1_q3, sixteen_bit_register_1_q4, sixteen_bit_register_1_q5,
       sixteen_bit_register_1_q6, sixteen_bit_register_1_q7, sixteen_bit_register_1_q8,
       sixteen_bit_register_1_q9, sixteen_bit_register_1_q10, sixteen_bit_register_1_q11,
       sixteen_bit_register_1_q12, sixteen_bit_register_1_q13, sixteen_bit_register_1_q14,
       sixteen_bit_register_1_q15, undriven, undriven_2, undriven_3, undriven_4, undriven_5, undriven_6,
       undriven_7, undriven_8, undriven_9, undriven_10, undriven_11, undriven_12, undriven_13, undriven_14,
       undriven_15;

  assign controlled_buffer_1_out = MAR_Bus_In_CS ? MAR_Bus_In : 1'bz;  // Controlled_Buffer controlled_buffer_1
  Sixteen_Bit_Register sixteen_bit_register_1 (
    .Q4(sixteen_bit_register_1_q4), .Q8(sixteen_bit_register_1_q8), .Q12(sixteen_bit_register_1_q12),
    .Q0(MAR_MM_In), .Q5(sixteen_bit_register_1_q5), .Q9(sixteen_bit_register_1_q9),
    .Q13(sixteen_bit_register_1_q13), .Q1(sixteen_bit_register_1_q1), .Q6(sixteen_bit_register_1_q6),
    .Q10(sixteen_bit_register_1_q10), .Q14(sixteen_bit_register_1_q14), .Q2(sixteen_bit_register_1_q2),
    .Q7(sixteen_bit_register_1_q7), .Q11(sixteen_bit_register_1_q11), .Q15(sixteen_bit_register_1_q15),
    .Q3(sixteen_bit_register_1_q3), .Clock(Clock), .Reset(Reset), .D0(controlled_buffer_1_out),
    .D4(undriven_12), .D8(undriven_8), .D12(undriven_4), .D1(undriven_15), .D5(undriven_11), .D9(undriven_7),
    .D13(undriven_3), .D2(undriven_14), .D6(undriven_10), .D10(undriven_6), .D14(undriven_2),
    .D3(undriven_13), .D7(undriven_9), .D11(undriven_5), .D15(undriven));
endmodule

module MDR (
  input  MDR_MM_In,
  input  READ_MM,
  input  MDR_Bus_In,
  input  MDR_Bus_In_CS,
  input  Clock,
  input  Reset,
  input  MDR_Bus_Out_CS,
  output MDR_MM_Out,
  output MDR_Bus_Out
);

  wire controlled_buffer_1_out, sixteen_bit_register_1_q1, sixteen_bit_register_1_q2,
       sixteen_bit_register_1_q3, sixteen_bit_register_1_q4, sixteen_bit_register_1_q5,
       sixteen_bit_register_1_q6, sixteen_bit_register_1_q7, sixteen_bit_register_1_q8,
       sixteen_bit_register_1_q9, sixteen_bit_register_1_q10, sixteen_bit_register_1_q11,
       sixteen_bit_register_1_q12, sixteen_bit_register_1_q13, sixteen_bit_register_1_q14,
       sixteen_bit_register_1_q15, undriven, undriven_2, undriven_3, undriven_4, undriven_5, undriven_6,
       undriven_7, undriven_8, undriven_9, undriven_10, undriven_11, undriven_12, undriven_13, undriven_14,
       undriven_15;

  assign controlled_buffer_1_out = READ_MM ? MDR_MM_In : 1'bz;  // Controlled_Buffer controlled_buffer_1
  assign controlled_buffer_1_out = MDR_Bus_In_CS ? MDR_Bus_In : 1'bz;  // Controlled_Buffer controlled_buffer_2
  Sixteen_Bit_Register sixteen_bit_register_1 (
    .Q4(sixteen_bit_register_1_q4), .Q8(sixteen_bit_register_1_q8), .Q12(sixteen_bit_register_1_q12),
    .Q0(MDR_MM_Out), .Q5(sixteen_bit_register_1_q5), .Q9(sixteen_bit_register_1_q9),
    .Q13(sixteen_bit_register_1_q13), .Q1(sixteen_bit_register_1_q1), .Q6(sixteen_bit_register_1_q6),
    .Q10(sixteen_bit_register_1_q10), .Q14(sixteen_bit_register_1_q14), .Q2(sixteen_bit_register_1_q2),
    .Q7(sixteen_bit_register_1_q7), .Q11(sixteen_bit_register_1_q11), .Q15(sixteen_bit_register_1_q15),
    .Q3(sixteen_bit_register_1_q3), .Clock(Clock), .Reset(Reset), .D0(controlled_buffer_1_out),
    .D4(undriven_12), .D8(undriven_8), .D12(undriven_4), .D1(undriven_15), .D5(undriven_11), .D9(undriven_7),
    .D13(undriven_3), .D2(undriven_14), .D6(undriven_10), .D10(undriven_6), .D14(undriven_2),
    .D3(undriven_13), .D7(undriven_9), .D11(undriven_5), .D15(undriven));
  assign MDR_Bus_Out = MDR_Bus_Out_CS ? MDR_MM_Out : 1'bz;  // Controlled_Buffer controlled_buffer_3
endmodule

module MM (
  input  MAR_in,
  input  Clock,
  input  Reset,
  input  MDR_in,
  input  WRITE_MM_CS,
  input  MDR_out,
  input  READ_MM_CS
);

  wire controlled_buffer_1_out, sixteen_bit_register_1_q0, sixteen_bit_register_1_q1,
       sixteen_bit_register_1_q2, sixteen_bit_register_1_q3, sixteen_bit_register_1_q4,
       sixteen_bit_register_1_q5, sixteen_bit_register_1_q6, sixteen_bit_register_1_q7,
       sixteen_bit_register_1_q8, sixteen_bit_register_1_q9, sixteen_bit_register_1_q10,
       sixteen_bit_register_1_q11, sixteen_bit_register_1_q12, sixteen_bit_register_1_q13,
       sixteen_bit_register_1_q14, sixteen_bit_register_1_q15, sixteen_bit_register_2_q0,
       sixteen_bit_register_2_q1, sixteen_bit_register_2_q2, sixteen_bit_register_2_q3,
       sixteen_bit_register_2_q4, sixteen_bit_register_2_q5, sixteen_bit_register_2_q6,
       sixteen_bit_register_2_q7, sixteen_bit_register_2_q8, sixteen_bit_register_2_q9,
       sixteen_bit_register_2_q10, sixteen_bit_register_2_q11, sixteen_bit_register_2_q12,
       sixteen_bit_register_2_q13, sixteen_bit_register_2_q14, sixteen_bit_register_2_q15,
       sixteen_bit_register_3_q0, sixteen_bit_register_3_q1, sixteen_bit_register_3_q2,
       sixteen_bit_register_3_q3, sixteen_bit_register_3_q4, sixteen_bit_register_3_q5,
       sixteen_bit_register_3_q6, sixteen_bit_register_3_q7, sixteen_bit_register_3_q8,
       sixteen_bit_register_3_q9, sixteen_bit_register_3_q10, sixteen_bit_register_3_q11,
       sixteen_bit_register_3_q12, sixteen_bit_register_3_q13, sixteen_bit_register_3_q14,
       sixteen_bit_register_3_q15, undriven, undriven_2, undriven_3, undriven_4, undriven_5, undriven_6,
       undriven_7, undriven_8, undriven_9, undriven_10, undriven_11, undriven_12, undriven_13, undriven_14,
       undriven_15, undriven_16, undriven_17, undriven_18, undriven_19, undriven_20, undriven_21,
       undriven_22, undriven_23, undriven_24, undriven_25, undriven_26, undriven_27, undriven_28,
       undriven_29, undriven_30, undriven_31, undriven_32, undriven_33, undriven_34, undriven_35,
       undriven_36, undriven_37, undriven_38, undriven_39, undriven_40, undriven_41, undriven_42,
       undriven_43, undriven_44, undriven_45, undriven_46;

  assign controlled_buffer_1_out = WRITE_MM_CS ? MDR_in : 1'bz;  // Controlled_Buffer controlled_buffer_1
  Sixteen_Bit_Register sixteen_bit_register_1 (
    .Q4(sixteen_bit_register_1_q4), .Q8(sixteen_bit_register_1_q8), .Q12(sixteen_bit_register_1_q12),
    .Q0(sixteen_bit_register_1_q0), .Q5(sixteen_bit_register_1_q5), .Q9(sixteen_bit_register_1_q9),
    .Q13(sixteen_bit_register_1_q13), .Q1(sixteen_bit_register_1_q1), .Q6(sixteen_bit_register_1_q6),
    .Q10(sixteen_bit_register_1_q10), .Q14(sixteen_bit_register_1_q14), .Q2(sixteen_bit_register_1_q2),
    .Q7(sixteen_bit_register_1_q7), .Q11(sixteen_bit_register_1_q11), .Q15(sixteen_bit_register_1_q15),
    .Q3(sixteen_bit_register_1_q3), .Clock(Clock), .Reset(Reset), .D0(MAR_in), .D4(undriven_35),
    .D8(undriven_23), .D12(undriven_11), .D1(undriven_44), .D5(undriven_32), .D9(undriven_20),
    .D13(undriven_8), .D2(undriven_41), .D6(undriven_29), .D10(undriven_17), .D14(undriven_5),
    .D3(undriven_38), .D7(undriven_26), .D11(undriven_14), .D15(undriven_2));
  Sixteen_Bit_Register sixteen_bit_register_2 (
    .Q4(sixteen_bit_register_2_q4), .Q8(sixteen_bit_register_2_q8), .Q12(sixteen_bit_register_2_q12),
    .Q0(sixteen_bit_register_2_q0), .Q5(sixteen_bit_register_2_q5), .Q9(sixteen_bit_register_2_q9),
    .Q13(sixteen_bit_register_2_q13), .Q1(sixteen_bit_register_2_q1), .Q6(sixteen_bit_register_2_q6),
    .Q10(sixteen_bit_register_2_q10), .Q14(sixteen_bit_register_2_q14), .Q2(sixteen_bit_register_2_q2),
    .Q7(sixteen_bit_register_2_q7), .Q11(sixteen_bit_register_2_q11), .Q15(sixteen_bit_register_2_q15),
    .Q3(sixteen_bit_register_2_q3), .Clock(Clock), .Reset(Reset), .D0(controlled_buffer_1_out),
    .D4(undriven_36), .D8(undriven_24), .D12(undriven_12), .D1(undriven_45), .D5(undriven_33),
    .D9(undriven_21), .D13(undriven_9), .D2(undriven_42), .D6(undriven_30), .D10(undriven_18),
    .D14(undriven_6), .D3(undriven_39), .D7(undriven_27), .D11(undriven_15), .D15(undriven_3));
  Sixteen_Bit_Register sixteen_bit_register_3 (
    .Q4(sixteen_bit_register_3_q4), .Q8(sixteen_bit_register_3_q8), .Q12(sixteen_bit_register_3_q12),
    .Q0(sixteen_bit_register_3_q0), .Q5(sixteen_bit_register_3_q5), .Q9(sixteen_bit_register_3_q9),
    .Q13(sixteen_bit_register_3_q13), .Q1(sixteen_bit_register_3_q1), .Q6(sixteen_bit_register_3_q6),
    .Q10(sixteen_bit_register_3_q10), .Q14(sixteen_bit_register_3_q14), .Q2(sixteen_bit_register_3_q2),
    .Q7(sixteen_bit_register_3_q7), .Q11(sixteen_bit_register_3_q11), .Q15(sixteen_bit_register_3_q15),
    .Q3(sixteen_bit_register_3_q3), .Clock(Clock), .Reset(Reset), .D0(undriven), .D4(undriven_37),
    .D8(undriven_25), .D12(undriven_13), .D1(undriven_46), .D5(undriven_34), .D9(undriven_22),
    .D13(undriven_10), .D2(undriven_43), .D6(undriven_31), .D10(undriven_19), .D14(undriven_7),
    .D3(undriven_40), .D7(undriven_28), .D11(undriven_16), .D15(undriven_4));
  assign MDR_out = READ_MM_CS ? sixteen_bit_register_3_q0 : 1'bz;  // Controlled_Buffer controlled_buffer_2
endmodule

module Carry_Lookahead_Generator (
  input  G15,
  input  G13,
  input  G11,
  input  G9,
  input  G7,
  input  G5,
  input  G3,
  input  G1,
  input  G14,
  input  G12,
  input  G10,
  input  G8,
  input  G6,
  input  G4,
  input  G2,
  input  G0,
  input  P15,
  input  P13,
  input  P11,
  input  P9,
  input  P7,
  input  P5,
  input  P3,
  input  P1,
  input  P14,
  input  P12,
  input  P10,
  input  P8,
  input  P6,
  input  P4,
  input  P2,
  input  P0,
  input  Carry_In,
  output C15,
  output C13,
  output C11,
  output C9,
  output C7,
  output C5,
  output C3,
  output C1,
  output C16,
  output C14,
  output C12,
  output C10,
  output C8,
  output C6,
  output C4,
  output C2
);

  Carry_Lookahead_One_Nibble carry_lookahead_one_nibble_1 (
    .C4(C16), .C3(C15), .C2(C14), .C1(C13), .G3(G15), .P3(P15), .G2(G14), .P2(P14), .G1(G13), .P1(P13),
    .G0(G12), .P0(P12), .Carry_In(C12));
  Carry_Lookahead_One_Nibble carry_lookahead_one_nibble_2 (
    .C4(C12), .C3(C11), .C2(C10), .C1(C9), .G3(G11), .P3(P11), .G2(G10), .P2(P10), .G1(G9), .P1(P9), .G0(G8),
    .P0(P8), .Carry_In(C8));
  Carry_Lookahead_One_Nibble carry_lookahead_one_nibble_3 (
    .C4(C8), .C3(C7), .C2(C6), .C1(C5), .G3(G7), .P3(P7), .G2(G6), .P2(P6), .G1(G5), .P1(P5), .G0(G4),
    .P0(P4), .Carry_In(C4));
  Carry_Lookahead_One_Nibble carry_lookahead_one_nibble_4 (
    .C4(C4), .C3(C3), .C2(C2), .C1(C1), .G3(G3), .P3(P3), .G2(G2), .P2(P2), .G1(G1), .P1(P1), .G0(G0),
    .P0(P0), .Carry_In(Carry_In));
endmodule

module Carry_Lookahead_One_Nibble (
  input  G3,
  input  P3,
  input  G2,
  input  P2,
  input  G1,
  input  P1,
  input  G0,
  input  P0,
  input  Carry_In,
  output C4,
  output C3,
  output C2,
  output C1
);

  wire and_1_out, and_2_out, and_3_out, and_4_out, and_5_out, and_6_out, and_7_out, and_8_out, and_9_out,
       and_10_out;

  and and_1 (and_1_out, G2, P3);
  or or_1 (C4, G3, and_1_out, and_2_out, and_3_out, and_4_out);
  and and_2 (and_2_out, P3, P2, G1);
  and and_3 (and_3_out, P3, P2, P1, G0);
  and and_4 (and_4_out, P3, P2, P1, P0, Carry_In);
  and and_5 (and_5_out, G1, P2);
  and and_6 (and_6_out, P2, P1, G0);
  or or_2 (C3, G2, and_5_out, and_6_out, and_7_out);
  and and_7 (and_7_out, P2, P1, P0, Carry_In);
  or or_3 (C2, G1, and_8_out, and_9_out);
  and and_8 (and_8_out, G0, P1);
  and and_9 (and_9_out, P1, P0, Carry_In);
  or or_4 (C1, G0, and_10_out);
  and and_10 (and_10_out, P0, Carry_In);
endmodule

module Carry_Lookahead_Adder_Subtractor (
  input  A15,
  input  B15,
  input  A14,
  input  B14,
  input  A13,
  input  B13,
  input  A12,
  input  B12,
  input  A11,
  input  B11,
  input  A10,
  input  B10,
  input  A9,
  input  B9,
  input  A8,
  input  B8,
  input  A7,
  input  B7,
  input  A6,
  input  B6,
  input  A5,
  input  B5,
  input  A4,
  input  B4,
  input  A3,
  input  B3,
  input  A2,
  input  B2,
  input  A1,
  input  B1,
  input  A0,
  input  B0,
  input  Mode,
  output S15,
  output S14,
  output S13,
  output S12,
  output S11,
  output S10,
  output S9,
  output S8,
  output S7,
  output S6,
  output S5,
  output S4,
  output S3,
  output S2,
  output S1,
  output S0
);

  wire and_1_out, and_2_out, and_3_out, and_4_out, and_5_out, and_6_out, and_7_out, and_8_out, and_9_out,
       and_10_out, and_11_out, and_12_out, and_13_out, and_14_out, and_15_out, and_16_out,
       carry_lookahead_generator_1_c1, carry_lookahead_generator_1_c2, carry_lookahead_generator_1_c3,
       carry_lookahead_generator_1_c4, carry_lookahead_generator_1_c5, carry_lookahead_generator_1_c6,
       carry_lookahead_generator_1_c7, carry_lookahead_generator_1_c8, carry_lookahead_generator_1_c9,
       carry_lookahead_generator_1_c10, carry_lookahead_generator_1_c11, carry_lookahead_generator_1_c12,
       carry_lookahead_generator_1_c13, carry_lookahead_generator_1_c14, carry_lookahead_generator_1_c15,
       xor_1_out, xor_2_out, xor_4_out, xor_5_out, xor_7_out, xor_8_out, xor_10_out, xor_11_out, xor_13_out,
       xor_14_out, xor_16_out, xor_17_out, xor_19_out, xor_20_out, xor_22_out, xor_23_out, xor_25_out,
       xor_26_out, xor_28_out, xor_29_out, xor_31_out, xor_32_out, xor_34_out, xor_35_out, xor_37_out,
       xor_38_out, xor_40_out, xor_41_out, xor_43_out, xor_44_out, xor_46_out, xor_47_out;

  and and_1 (and_1_out, A15, B15);
  xor xor_1 (xor_1_out, B15, Mode);
  xor xor_2 (xor_2_out, A15, xor_1_out);
  and and_2 (and_2_out, A14, B14);
  xor xor_3 (S15, xor_2_out, carry_lookahead_generator_1_c15);
  xor xor_4 (xor_4_out, B14, Mode);
  xor xor_5 (xor_5_out, A14, xor_4_out);
  and and_3 (and_3_out, A13, B13);
  xor xor_6 (S14, xor_5_out, carry_lookahead_generator_1_c14);
  xor xor_7 (xor_7_out, B13, Mode);
  and and_4 (and_4_out, A12, B12);
  xor xor_8 (xor_8_out, A13, xor_7_out);
  xor xor_9 (S13, xor_8_out, carry_lookahead_generator_1_c13);
  xor xor_10 (xor_10_out, B12, Mode);
  xor xor_11 (xor_11_out, A12, xor_10_out);
  and and_5 (and_5_out, A11, B11);
  xor xor_12 (S12, xor_11_out, carry_lookahead_generator_1_c12);
  xor xor_13 (xor_13_out, B11, Mode);
  xor xor_14 (xor_14_out, A11, xor_13_out);
  and and_6 (and_6_out, A10, B10);
  xor xor_15 (S11, xor_14_out, carry_lookahead_generator_1_c11);
  xor xor_16 (xor_16_out, B10, Mode);
  xor xor_17 (xor_17_out, A10, xor_16_out);
  and and_7 (and_7_out, A9, B9);
  xor xor_18 (S10, xor_17_out, carry_lookahead_generator_1_c10);
  xor xor_19 (xor_19_out, B9, Mode);
  xor xor_20 (xor_20_out, A9, xor_19_out);
  and and_8 (and_8_out, A8, B8);
  Carry_Lookahead_Generator carry_lookahead_generator_1 (
    .C15(carry_lookahead_generator_1_c15), .C14(carry_lookahead_generator_1_c14),
    .C13(carry_lookahead_generator_1_c13), .C12(carry_lookahead_generator_1_c12),
    .C11(carry_lookahead_generator_1_c11), .C10(carry_lookahead_generator_1_c10),
    .C9(carry_lookahead_generator_1_c9), .C8(carry_lookahead_generator_1_c8),
    .C7(carry_lookahead_generator_1_c7), .C6(carry_lookahead_generator_1_c6),
    .C5(carry_lookahead_generator_1_c5), .C4(carry_lookahead_generator_1_c4),
    .C3(carry_lookahead_generator_1_c3), .C2(carry_lookahead_generator_1_c2),
    .C1(carry_lookahead_generator_1_c1), .G15(and_1_out), .P15(xor_2_out), .G14(and_2_out), .P14(xor_5_out),
    .G13(and_3_out), .P13(xor_8_out), .G12(and_4_out), .P12(xor_11_out), .G11(and_5_out), .P11(xor_14_out),
    .G10(and_6_out), .P10(xor_17_out), .G9(and_7_out), .P9(xor_20_out), .G8(and_8_out), .P8(xor_23_out),
    .G7(and_9_out), .P7(xor_26_out), .G6(and_10_out), .P6(xor_29_out), .G5(and_11_out), .P5(xor_32_out),
    .G4(and_12_out), .P4(xor_35_out), .G3(and_13_out), .P3(xor_38_out), .G2(and_14_out), .P2(xor_41_out),
    .G1(and_15_out), .P1(xor_44_out), .G0(and_16_out), .P0(xor_47_out));  // open: C16, Carry_In
  xor xor_21 (S9, xor_20_out, carry_lookahead_generator_1_c9);
  xor xor_22 (xor_22_out, B8, Mode);
  xor xor_23 (xor_23_out, A8, xor_22_out);
  and and_9 (and_9_out, A7, B7);
  xor xor_24 (S8, xor_23_out, carry_lookahead_generator_1_c8);
  xor xor_25 (xor_25_out, B7, Mode);
  xor xor_26 (xor_26_out, A7, xor_25_out);
  and and_10 (and_10_out, A6, B6);
  xor xor_27 (S7, xor_26_out, carry_lookahead_generator_1_c7);
  xor xor_28 (xor_28_out, B6, Mode);
  xor xor_29 (xor_29_out, A6, xor_28_out);
  and and_11 (and_11_out, A5, B5);
  xor xor_30 (S6, xor_29_out, carry_lookahead_generator_1_c6);
  xor xor_31 (xor_31_out, B5, Mode);
  xor xor_32 (xor_32_out, A5, xor_31_out);
  and and_12 (and_12_out, A4, B4);
  xor xor_33 (S5, xor_32_out, carry_lookahead_generator_1_c5);
  xor xor_34 (xor_34_out, B4, Mode);
  xor xor_35 (xor_35_out, A4, xor_34_out);
  and and_13 (and_13_out, A3, B3);
  xor xor_36 (S4, xor_35_out, carry_lookahead_generator_1_c4);
  xor xor_37 (xor_37_out, B3, Mode);
  xor xor_38 (xor_38_out, A3, xor_37_out);
  and and_14 (and_14_out, A2, B2);
  xor xor_39 (S3, xor_38_out, carry_lookahead_generator_1_c3);
  xor xor_40 (xor_40_out, B2, Mode);
  xor xor_41 (xor_41_out, A2, xor_40_out);
  and and_15 (and_15_out, A1, B1);
  xor xor_42 (S2, xor_41_out, carry_lookahead_generator_1_c2);
  xor xor_43 (xor_43_out, B1, Mode);
  xor xor_44 (xor_44_out, A1, xor_43_out);
  and and_16 (and_16_out, A0, B0);
  xor xor_45 (S1, xor_44_out, carry_lookahead_generator_1_c1);
  xor xor_46 (xor_46_out, B0, Mode);
  xor xor_47 (xor_47_out, A0, xor_46_out);
  xor xor_48 (S0, xor_47_out, Mode);
endmodule

module One_Bit_Left_Shift (
  input  A15,
  input  A14,
  input  A13,
  input  A12,
  input  A11,
  input  A10,
  input  A9,
  input  A8,
  input  A7,
  input  A6,
  input  A5,
  input  A4,
  input  A3,
  input  A2,
  input  A1,
  input  A0,
  input  S0,
  output Z15,
  output Z14,
  output Z13,
  output Z12,
  output Z11,
  output Z10,
  output Z9,
  output Z8,
  output Z7,
  output Z6,
  output Z5,
  output Z4,
  output Z3,
  output Z2,
  output Z1,
  output Z0
);

  Multiplexer #(.enable("false")) multiplexer_1 (.in0(A15), .in1(A14), .out(Z15), .sel(S0));
  Multiplexer #(.enable("false")) multiplexer_2 (.in0(A14), .in1(A13), .out(Z14), .sel(S0));
  Multiplexer #(.enable("false")) multiplexer_3 (.in0(A13), .in1(A12), .out(Z13), .sel(S0));
  Multiplexer #(.enable("false")) multiplexer_4 (.in0(A12), .in1(A11), .out(Z12), .sel(S0));
  Multiplexer #(.enable("false")) multiplexer_5 (.in0(A11), .in1(A10), .out(Z11), .sel(S0));
  Multiplexer #(.enable("false")) multiplexer_6 (.in0(A10), .in1(A9), .out(Z10), .sel(S0));
  Multiplexer #(.enable("false")) multiplexer_7 (.in0(A9), .in1(A8), .out(Z9), .sel(S0));
  Multiplexer #(.enable("false")) multiplexer_8 (.in0(A8), .in1(A7), .out(Z8), .sel(S0));
  Multiplexer #(.enable("false")) multiplexer_9 (.in0(A7), .in1(A6), .out(Z7), .sel(S0));
  Multiplexer #(.enable("false")) multiplexer_10 (.in0(A6), .in1(A5), .out(Z6), .sel(S0));
  Multiplexer #(.enable("false")) multiplexer_11 (.in0(A5), .in1(A4), .out(Z5), .sel(S0));
  Multiplexer #(.enable("false")) multiplexer_12 (.in0(A3), .in1(A2), .out(Z3), .sel(S0));
  Multiplexer #(.enable("false")) multiplexer_13 (.in0(A4), .in1(A3), .out(Z4), .sel(S0));
  Multiplexer #(.enable("false")) multiplexer_14 (.in0(A2), .in1(A1), .out(Z2), .sel(S0));
  Multiplexer #(.enable("false")) multiplexer_15 (.in0(A1), .in1(A0), .out(Z1), .sel(S0));
  Multiplexer #(.enable("false")) multiplexer_16 (.in0(A0), .in1(1'b0), .out(Z0), .sel(S0));
endmodule

module Four_Bit_Left_Shift (
  input  A15,
  input  A14,
  input  A13,
  input  A12,
  input  A11,
  input  A10,
  input  A9,
  input  A8,
  input  A7,
  input  A6,
  input  A5,
  input  A4,
  input  A3,
  input  A2,
  input  A1,
  input  A0,
  input  S0,
  input  S1,
  input  S2,
  input  S3,
  output Z15,
  output Z14,
  output Z13,
  output Z12,
  output Z11,
  output Z10,
  output Z9,
  output Z8,
  output Z7,
  output Z6,
  output Z5,
  output Z4,
  output Z3,
  output Z2,
  output Z1,
  output Z0
);

  wire multiplexer_1_out, multiplexer_2_out, multiplexer_3_out, multiplexer_5_out, multiplexer_6_out,
       multiplexer_7_out, multiplexer_8_out, multiplexer_9_out, multiplexer_10_out, multiplexer_12_out,
       multiplexer_13_out, multiplexer_14_out, multiplexer_15_out, multiplexer_18_out, multiplexer_19_out,
       multiplexer_20_out, multiplexer_21_out, multiplexer_22_out, multiplexer_25_out, multiplexer_26_out,
       multiplexer_27_out, multiplexer_28_out, multiplexer_29_out, multiplexer_31_out, multiplexer_32_out,
       multiplexer_33_out, multiplexer_34_out, multiplexer_37_out, multiplexer_38_out, multiplexer_39_out,
       multiplexer_40_out, multiplexer_41_out, multiplexer_42_out, multiplexer_44_out, multiplexer_45_out,
       multiplexer_46_out, multiplexer_47_out, multiplexer_50_out, multiplexer_51_out, multiplexer_52_out,
       multiplexer_53_out, multiplexer_54_out, multiplexer_57_out, multiplexer_58_out, multiplexer_59_out,
       multiplexer_60_out, multiplexer_61_out, multiplexer_63_out;

  Multiplexer #(.enable("false")) multiplexer_1 (.in0(A15), .in1(A14), .out(multiplexer_1_out), .sel(S0));
  Multiplexer #(.enable("false")) multiplexer_2 (
    .in0(multiplexer_1_out), .in1(multiplexer_6_out), .out(multiplexer_2_out), .sel(S1));
  Multiplexer #(.enable("false")) multiplexer_3 (
    .in0(multiplexer_2_out), .in1(multiplexer_19_out), .out(multiplexer_3_out), .sel(S2));
  Multiplexer #(.enable("false")) multiplexer_4 (
    .in0(multiplexer_3_out), .in1(multiplexer_34_out), .out(Z15), .sel(S3));
  Multiplexer #(.enable("false")) multiplexer_5 (.in0(A14), .in1(A13), .out(multiplexer_5_out), .sel(S0));
  Multiplexer #(.enable("false")) multiplexer_6 (.in0(A13), .in1(A12), .out(multiplexer_6_out), .sel(S0));
  Multiplexer #(.enable("false")) multiplexer_7 (
    .in0(multiplexer_5_out), .in1(multiplexer_12_out), .out(multiplexer_7_out), .sel(S1));
  Multiplexer #(.enable("false")) multiplexer_8 (
    .in0(multiplexer_6_out), .in1(multiplexer_13_out), .out(multiplexer_8_out), .sel(S1));
  Multiplexer #(.enable("false")) multiplexer_9 (
    .in0(multiplexer_7_out), .in1(multiplexer_20_out), .out(multiplexer_9_out), .sel(S2));
  Multiplexer #(.enable("false")) multiplexer_10 (
    .in0(multiplexer_8_out), .in1(multiplexer_27_out), .out(multiplexer_10_out), .sel(S2));
  Multiplexer #(.enable("false")) multiplexer_11 (
    .in0(multiplexer_9_out), .in1(multiplexer_41_out), .out(Z14), .sel(S3));
  Multiplexer #(.enable("false")) multiplexer_12 (.in0(A12), .in1(A11), .out(multiplexer_12_out), .sel(S0));
  Multiplexer #(.enable("false")) multiplexer_13 (.in0(A11), .in1(A10), .out(multiplexer_13_out), .sel(S0));
  Multiplexer #(.enable("false")) multiplexer_14 (
    .in0(multiplexer_12_out), .in1(multiplexer_18_out), .out(multiplexer_14_out), .sel(S1));
  Multiplexer #(.enable("false")) multiplexer_15 (
    .in0(multiplexer_14_out), .in1(multiplexer_28_out), .out(multiplexer_15_out), .sel(S2));
  Multiplexer #(.enable("false")) multiplexer_16 (.in0(multiplexer_10_out), .in1(1'b0), .out(Z13), .sel(S3));
  Multiplexer #(.enable("false")) multiplexer_17 (
    .in0(multiplexer_15_out), .in1(multiplexer_47_out), .out(Z12), .sel(S3));
  Multiplexer #(.enable("false")) multiplexer_18 (.in0(A10), .in1(A9), .out(multiplexer_18_out), .sel(S0));
  Multiplexer #(.enable("false")) multiplexer_19 (
    .in0(multiplexer_13_out), .in1(multiplexer_25_out), .out(multiplexer_19_out), .sel(S1));
  Multiplexer #(.enable("false")) multiplexer_20 (
    .in0(multiplexer_18_out), .in1(multiplexer_26_out), .out(multiplexer_20_out), .sel(S1));
  Multiplexer #(.enable("false")) multiplexer_21 (
    .in0(multiplexer_19_out), .in1(multiplexer_32_out), .out(multiplexer_21_out), .sel(S2));
  Multiplexer #(.enable("false")) multiplexer_22 (
    .in0(multiplexer_20_out), .in1(multiplexer_39_out), .out(multiplexer_22_out), .sel(S2));
  Multiplexer #(.enable("false")) multiplexer_23 (
    .in0(multiplexer_21_out), .in1(multiplexer_53_out), .out(Z11), .sel(S3));
  Multiplexer #(.enable("false")) multiplexer_24 (
    .in0(multiplexer_22_out), .in1(multiplexer_54_out), .out(Z10), .sel(S3));
  Multiplexer #(.enable("false")) multiplexer_25 (.in0(A9), .in1(A8), .out(multiplexer_25_out), .sel(S0));
  Multiplexer #(.enable("false")) multiplexer_26 (.in0(A8), .in1(A7), .out(multiplexer_26_out), .sel(S0));
  Multiplexer #(.enable("false")) multiplexer_27 (
    .in0(multiplexer_25_out), .in1(multiplexer_31_out), .out(multiplexer_27_out), .sel(S1));
  Multiplexer #(.enable("false")) multiplexer_28 (
    .in0(multiplexer_26_out), .in1(multiplexer_37_out), .out(multiplexer_28_out), .sel(S1));
  Multiplexer #(.enable("false")) multiplexer_29 (
    .in0(multiplexer_27_out), .in1(multiplexer_40_out), .out(multiplexer_29_out), .sel(S2));
  Multiplexer #(.enable("false")) multiplexer_30 (
    .in0(multiplexer_29_out), .in1(multiplexer_61_out), .out(Z9), .sel(S3));
  Multiplexer #(.enable("false")) multiplexer_31 (.in0(A7), .in1(A6), .out(multiplexer_31_out), .sel(S0));
  Multiplexer #(.enable("false")) multiplexer_32 (
    .in0(multiplexer_31_out), .in1(multiplexer_38_out), .out(multiplexer_32_out), .sel(S1));
  Multiplexer #(.enable("false")) multiplexer_33 (
    .in0(multiplexer_28_out), .in1(multiplexer_46_out), .out(multiplexer_33_out), .sel(S2));
  Multiplexer #(.enable("false")) multiplexer_34 (
    .in0(multiplexer_32_out), .in1(multiplexer_51_out), .out(multiplexer_34_out), .sel(S2));
  Multiplexer #(.enable("false")) multiplexer_35 (
    .in0(multiplexer_33_out), .in1(multiplexer_63_out), .out(Z8), .sel(S3));
  Multiplexer #(.enable("false")) multiplexer_36 (.in0(multiplexer_34_out), .in1(1'b0), .out(Z7), .sel(S3));
  Multiplexer #(.enable("false")) multiplexer_37 (.in0(A6), .in1(A5), .out(multiplexer_37_out), .sel(S0));
  Multiplexer #(.enable("false")) multiplexer_38 (.in0(A5), .in1(A4), .out(multiplexer_38_out), .sel(S0));
  Multiplexer #(.enable("false")) multiplexer_39 (
    .in0(multiplexer_37_out), .in1(multiplexer_45_out), .out(multiplexer_39_out), .sel(S1));
  Multiplexer #(.enable("false")) multiplexer_40 (
    .in0(multiplexer_38_out), .in1(multiplexer_44_out), .out(multiplexer_40_out), .sel(S1));
  Multiplexer #(.enable("false")) multiplexer_41 (
    .in0(multiplexer_39_out), .in1(multiplexer_52_out), .out(multiplexer_41_out), .sel(S2));
  Multiplexer #(.enable("false")) multiplexer_42 (
    .in0(multiplexer_40_out), .in1(multiplexer_59_out), .out(multiplexer_42_out), .sel(S2));
  Multiplexer #(.enable("false")) multiplexer_43 (.in0(multiplexer_41_out), .in1(1'b0), .out(Z6), .sel(S3));
  Multiplexer #(.enable("false")) multiplexer_44 (.in0(A3), .in1(A2), .out(multiplexer_44_out), .sel(S0));
  Multiplexer #(.enable("false")) multiplexer_45 (.in0(A4), .in1(A3), .out(multiplexer_45_out), .sel(S0));
  Multiplexer #(.enable("false")) multiplexer_46 (
    .in0(multiplexer_45_out), .in1(multiplexer_50_out), .out(multiplexer_46_out), .sel(S1));
  Multiplexer #(.enable("false")) multiplexer_47 (
    .in0(multiplexer_46_out), .in1(multiplexer_60_out), .out(multiplexer_47_out), .sel(S2));
  Multiplexer #(.enable("false")) multiplexer_48 (.in0(multiplexer_47_out), .in1(1'b0), .out(Z4), .sel(S3));
  Multiplexer #(.enable("false")) multiplexer_49 (.in0(multiplexer_42_out), .in1(1'b0), .out(Z5), .sel(S3));
  Multiplexer #(.enable("false")) multiplexer_50 (.in0(A2), .in1(A1), .out(multiplexer_50_out), .sel(S0));
  Multiplexer #(.enable("false")) multiplexer_51 (
    .in0(multiplexer_44_out), .in1(multiplexer_57_out), .out(multiplexer_51_out), .sel(S1));
  Multiplexer #(.enable("false")) multiplexer_52 (
    .in0(multiplexer_50_out), .in1(multiplexer_58_out), .out(multiplexer_52_out), .sel(S1));
  Multiplexer #(.enable("false")) multiplexer_53 (
    .in0(multiplexer_51_out), .in1(1'b0), .out(multiplexer_53_out), .sel(S2));
  Multiplexer #(.enable("false")) multiplexer_54 (
    .in0(multiplexer_52_out), .in1(1'b0), .out(multiplexer_54_out), .sel(S2));
  Multiplexer #(.enable("false")) multiplexer_55 (.in0(multiplexer_53_out), .in1(1'b0), .out(Z3), .sel(S3));
  Multiplexer #(.enable("false")) multiplexer_56 (.in0(multiplexer_54_out), .in1(1'b0), .out(Z2), .sel(S3));
  Multiplexer #(.enable("false")) multiplexer_57 (.in0(A1), .in1(A0), .out(multiplexer_57_out), .sel(S0));
  Multiplexer #(.enable("false")) multiplexer_58 (.in0(A0), .in1(1'b0), .out(multiplexer_58_out), .sel(S0));
  Multiplexer #(.enable("false")) multiplexer_59 (
    .in0(multiplexer_57_out), .in1(1'b0), .out(multiplexer_59_out), .sel(S1));
  Multiplexer #(.enable("false")) multiplexer_60 (
    .in0(multiplexer_58_out), .in1(1'b0), .out(multiplexer_60_out), .sel(S1));
  Multiplexer #(.enable("false")) multiplexer_61 (
    .in0(multiplexer_59_out), .in1(1'b0), .out(multiplexer_61_out), .sel(S2));
  Multiplexer #(.enable("false")) multiplexer_62 (.in0(multiplexer_61_out), .in1(1'b0), .out(Z1), .sel(S3));
  Multiplexer #(.enable("false")) multiplexer_63 (
    .in0(multiplexer_60_out), .in1(1'b0), .out(multiplexer_63_out), .sel(S2));
  Multiplexer #(.enable("false")) multiplexer_64 (.in0(multiplexer_63_out), .in1(1'b0), .out(Z0), .sel(S3));
endmodule

module Four_Bit_Right_Shift (
  input  A15,
  input  A14,
  input  A13,
  input  A12,
  input  A11,
  input  A10,
  input  A9,
  input  A8,
  input  A7,
  input  A6,
  input  A5,
  input  A4,
  input  A3,
  input  A2,
  input  A1,
  input  A0,
  input  S0,
  input  S1,
  input  S2,
  input  S3,
  output Z15,
  output Z14,
  output Z13,
  output Z12,
  output Z11,
  output Z10,
  output Z9,
  output Z8,
  output Z7,
  output Z6,
  output Z5,
  output Z4,
  output Z3,
  output Z2,
  output Z1,
  output Z0
);

  wire multiplexer_1_out, multiplexer_2_out, multiplexer_3_out, multiplexer_4_out, multiplexer_5_out,
       multiplexer_8_out, multiplexer_9_out, multiplexer_10_out, multiplexer_11_out, multiplexer_14_out,
       multiplexer_15_out, multiplexer_16_out, multiplexer_17_out, multiplexer_18_out, multiplexer_19_out,
       multiplexer_21_out, multiplexer_22_out, multiplexer_23_out, multiplexer_24_out, multiplexer_27_out,
       multiplexer_28_out, multiplexer_29_out, multiplexer_30_out, multiplexer_31_out, multiplexer_33_out,
       multiplexer_34_out, multiplexer_35_out, multiplexer_36_out, multiplexer_37_out, multiplexer_40_out,
       multiplexer_41_out, multiplexer_42_out, multiplexer_43_out, multiplexer_46_out, multiplexer_47_out,
       multiplexer_48_out, multiplexer_49_out, multiplexer_50_out, multiplexer_51_out, multiplexer_53_out,
       multiplexer_54_out, multiplexer_55_out, multiplexer_56_out, multiplexer_59_out, multiplexer_60_out,
       multiplexer_61_out, multiplexer_62_out, multiplexer_63_out, not_1_out, not_2_out, not_3_out, not_4_out;

  Multiplexer #(.enable("false")) multiplexer_1 (.in0(A15), .in1(A15), .out(multiplexer_1_out), .sel(not_1_out));
  Multiplexer #(.enable("false")) multiplexer_2 (
    .in0(A15), .in1(multiplexer_1_out), .out(multiplexer_2_out), .sel(not_2_out));
  Multiplexer #(.enable("false")) multiplexer_3 (
    .in0(A15), .in1(multiplexer_8_out), .out(multiplexer_3_out), .sel(not_2_out));
  Multiplexer #(.enable("false")) multiplexer_4 (
    .in0(A15), .in1(multiplexer_2_out), .out(multiplexer_4_out), .sel(not_3_out));
  Multiplexer #(.enable("false")) multiplexer_5 (
    .in0(A15), .in1(multiplexer_3_out), .out(multiplexer_5_out), .sel(not_3_out));
  Multiplexer #(.enable("false")) multiplexer_6 (.in0(A15), .in1(multiplexer_4_out), .out(Z15), .sel(not_4_out));
  Multiplexer #(.enable("false")) multiplexer_7 (.in0(A15), .in1(multiplexer_5_out), .out(Z14), .sel(not_4_out));
  Multiplexer #(.enable("false")) multiplexer_8 (.in0(A15), .in1(A14), .out(multiplexer_8_out), .sel(not_1_out));
  Multiplexer #(.enable("false")) multiplexer_9 (.in0(A14), .in1(A13), .out(multiplexer_9_out), .sel(not_1_out));
  Multiplexer #(.enable("false")) multiplexer_10 (
    .in0(multiplexer_1_out), .in1(multiplexer_9_out), .out(multiplexer_10_out), .sel(not_2_out));
  Multiplexer #(.enable("false")) multiplexer_11 (
    .in0(A15), .in1(multiplexer_10_out), .out(multiplexer_11_out), .sel(not_3_out));
  Multiplexer #(.enable("false")) multiplexer_12 (.in0(A15), .in1(multiplexer_11_out), .out(Z13), .sel(not_4_out));
  Multiplexer #(.enable("false")) multiplexer_13 (.in0(A15), .in1(multiplexer_18_out), .out(Z12), .sel(not_4_out));
  Multiplexer #(.enable("false")) multiplexer_14 (.in0(A13), .in1(A12), .out(multiplexer_14_out), .sel(not_1_out));
  Multiplexer #(.enable("false")) multiplexer_15 (.in0(A12), .in1(A11), .out(multiplexer_15_out), .sel(not_1_out));
  Multiplexer #(.enable("false")) multiplexer_16 (
    .in0(multiplexer_8_out), .in1(multiplexer_14_out), .out(multiplexer_16_out), .sel(not_2_out));
  Multiplexer #(.enable("false")) multiplexer_17 (
    .in0(multiplexer_9_out), .in1(multiplexer_15_out), .out(multiplexer_17_out), .sel(not_2_out));
  Multiplexer #(.enable("false")) multiplexer_18 (
    .in0(A15), .in1(multiplexer_16_out), .out(multiplexer_18_out), .sel(not_3_out));
  Multiplexer #(.enable("false")) multiplexer_19 (
    .in0(multiplexer_2_out), .in1(multiplexer_17_out), .out(multiplexer_19_out), .sel(not_3_out));
  Multiplexer #(.enable("false")) multiplexer_20 (.in0(A15), .in1(multiplexer_19_out), .out(Z11), .sel(not_4_out));
  Multiplexer #(.enable("false")) multiplexer_21 (.in0(A11), .in1(A10), .out(multiplexer_21_out), .sel(not_1_out));
  Multiplexer #(.enable("false")) multiplexer_22 (
    .in0(multiplexer_14_out), .in1(multiplexer_21_out), .out(multiplexer_22_out), .sel(not_2_out));
  Multiplexer #(.enable("false")) multiplexer_23 (
    .in0(multiplexer_3_out), .in1(multiplexer_22_out), .out(multiplexer_23_out), .sel(not_3_out));
  Multiplexer #(.enable("false")) multiplexer_24 (
    .in0(multiplexer_10_out), .in1(multiplexer_29_out), .out(multiplexer_24_out), .sel(not_3_out));
  Multiplexer #(.enable("false")) multiplexer_25 (.in0(A15), .in1(multiplexer_23_out), .out(Z10), .sel(not_4_out));
  Multiplexer #(.enable("false")) multiplexer_26 (.in0(A15), .in1(multiplexer_24_out), .out(Z9), .sel(not_4_out));
  Multiplexer #(.enable("false")) multiplexer_27 (.in0(A10), .in1(A9), .out(multiplexer_27_out), .sel(not_1_out));
  Multiplexer #(.enable("false")) multiplexer_28 (.in0(A9), .in1(A8), .out(multiplexer_28_out), .sel(not_1_out));
  Multiplexer #(.enable("false")) multiplexer_29 (
    .in0(multiplexer_15_out), .in1(multiplexer_27_out), .out(multiplexer_29_out), .sel(not_2_out));
  Multiplexer #(.enable("false")) multiplexer_30 (
    .in0(multiplexer_21_out), .in1(multiplexer_28_out), .out(multiplexer_30_out), .sel(not_2_out));
  Multiplexer #(.enable("false")) multiplexer_31 (
    .in0(multiplexer_16_out), .in1(multiplexer_30_out), .out(multiplexer_31_out), .sel(not_3_out));
  Multiplexer #(.enable("false")) multiplexer_32 (.in0(A15), .in1(multiplexer_31_out), .out(Z8), .sel(not_4_out));
  Multiplexer #(.enable("false")) multiplexer_33 (.in0(A8), .in1(A7), .out(multiplexer_33_out), .sel(not_1_out));
  Multiplexer #(.enable("false")) multiplexer_34 (
    .in0(multiplexer_27_out), .in1(multiplexer_33_out), .out(multiplexer_34_out), .sel(not_2_out));
  Multiplexer #(.enable("false")) multiplexer_35 (
    .in0(multiplexer_28_out), .in1(multiplexer_40_out), .out(multiplexer_35_out), .sel(not_2_out));
  Multiplexer #(.enable("false")) multiplexer_36 (
    .in0(multiplexer_17_out), .in1(multiplexer_34_out), .out(multiplexer_36_out), .sel(not_3_out));
  Multiplexer #(.enable("false")) multiplexer_37 (
    .in0(multiplexer_22_out), .in1(multiplexer_35_out), .out(multiplexer_37_out), .sel(not_3_out));
  Multiplexer #(.enable("false")) multiplexer_38 (
    .in0(multiplexer_4_out), .in1(multiplexer_36_out), .out(Z7), .sel(not_4_out));
  Multiplexer #(.enable("false")) multiplexer_39 (
    .in0(multiplexer_5_out), .in1(multiplexer_37_out), .out(Z6), .sel(not_4_out));
  Multiplexer #(.enable("false")) multiplexer_40 (.in0(A7), .in1(A6), .out(multiplexer_40_out), .sel(not_1_out));
  Multiplexer #(.enable("false")) multiplexer_41 (.in0(A6), .in1(A5), .out(multiplexer_41_out), .sel(not_1_out));
  Multiplexer #(.enable("false")) multiplexer_42 (
    .in0(multiplexer_33_out), .in1(multiplexer_41_out), .out(multiplexer_42_out), .sel(not_2_out));
  Multiplexer #(.enable("false")) multiplexer_43 (
    .in0(multiplexer_29_out), .in1(multiplexer_42_out), .out(multiplexer_43_out), .sel(not_3_out));
  Multiplexer #(.enable("false")) multiplexer_44 (
    .in0(multiplexer_11_out), .in1(multiplexer_43_out), .out(Z5), .sel(not_4_out));
  Multiplexer #(.enable("false")) multiplexer_45 (
    .in0(multiplexer_18_out), .in1(multiplexer_51_out), .out(Z4), .sel(not_4_out));
  Multiplexer #(.enable("false")) multiplexer_46 (.in0(A4), .in1(A3), .out(multiplexer_46_out), .sel(not_1_out));
  Multiplexer #(.enable("false")) multiplexer_47 (.in0(A5), .in1(A4), .out(multiplexer_47_out), .sel(not_1_out));
  Multiplexer #(.enable("false")) multiplexer_48 (
    .in0(multiplexer_41_out), .in1(multiplexer_46_out), .out(multiplexer_48_out), .sel(not_2_out));
  Multiplexer #(.enable("false")) multiplexer_49 (
    .in0(multiplexer_40_out), .in1(multiplexer_47_out), .out(multiplexer_49_out), .sel(not_2_out));
  Multiplexer #(.enable("false")) multiplexer_50 (
    .in0(multiplexer_34_out), .in1(multiplexer_48_out), .out(multiplexer_50_out), .sel(not_3_out));
  Multiplexer #(.enable("false")) multiplexer_51 (
    .in0(multiplexer_30_out), .in1(multiplexer_49_out), .out(multiplexer_51_out), .sel(not_3_out));
  Multiplexer #(.enable("false")) multiplexer_52 (
    .in0(multiplexer_19_out), .in1(multiplexer_50_out), .out(Z3), .sel(not_4_out));
  Multiplexer #(.enable("false")) multiplexer_53 (.in0(A3), .in1(A2), .out(multiplexer_53_out), .sel(not_1_out));
  Multiplexer #(.enable("false")) multiplexer_54 (
    .in0(multiplexer_47_out), .in1(multiplexer_53_out), .out(multiplexer_54_out), .sel(not_2_out));
  Multiplexer #(.enable("false")) multiplexer_55 (
    .in0(multiplexer_35_out), .in1(multiplexer_54_out), .out(multiplexer_55_out), .sel(not_3_out));
  Multiplexer #(.enable("false")) multiplexer_56 (
    .in0(multiplexer_42_out), .in1(multiplexer_61_out), .out(multiplexer_56_out), .sel(not_3_out));
  Multiplexer #(.enable("false")) multiplexer_57 (
    .in0(multiplexer_23_out), .in1(multiplexer_55_out), .out(Z2), .sel(not_4_out));
  Multiplexer #(.enable("false")) multiplexer_58 (
    .in0(multiplexer_24_out), .in1(multiplexer_56_out), .out(Z1), .sel(not_4_out));
  Multiplexer #(.enable("false")) multiplexer_59 (.in0(A2), .in1(A1), .out(multiplexer_59_out), .sel(not_1_out));
  Multiplexer #(.enable("false")) multiplexer_60 (.in0(A1), .in1(A0), .out(multiplexer_60_out), .sel(not_1_out));
  Multiplexer #(.enable("false")) multiplexer_61 (
    .in0(multiplexer_46_out), .in1(multiplexer_59_out), .out(multiplexer_61_out), .sel(not_2_out));
  Multiplexer #(.enable("false")) multiplexer_62 (
    .in0(multiplexer_53_out), .in1(multiplexer_60_out), .out(multiplexer_62_out), .sel(not_2_out));
  Multiplexer #(.enable("false")) multiplexer_63 (
    .in0(multiplexer_49_out), .in1(multiplexer_62_out), .out(multiplexer_63_out), .sel(not_3_out));
  Multiplexer #(.enable("false")) multiplexer_64 (
    .in0(multiplexer_31_out), .in1(multiplexer_63_out), .out(Z0), .sel(not_4_out));
  not not_1 (not_1_out, S0);
  not not_2 (not_2_out, S1);
  not not_3 (not_3_out, S2);
  not not_4 (not_4_out, S3);
endmodule

module ALU (
  input  Bus_In,
  input  Y_In,
  input  Bus_In_CS,
  input  IR_Shift,
  input  IR_Shift_0_CS,
  input  S0,
  input  S1,
  input  S2,
  input  S3,
  input  ALU_Inc_2,
  input  OP0,
  input  OP1,
  input  ALU_Opcode_Task,
  input  OP2,
  input  OP3,
  input  OP4,
  input  ALU_ADD,
  input  OP5,
  input  ALU_NOT,
  output Z_Out
);

  wire ALU_AND, ALU_LS, ALU_OR, ALU_PASS, ALU_RS, ALU_SUB, carry_lookahead_adder_subtractor_1_s2,
       carry_lookahead_adder_subtractor_1_s3, carry_lookahead_adder_subtractor_1_s4,
       carry_lookahead_adder_subtractor_1_s5, carry_lookahead_adder_subtractor_1_s6,
       carry_lookahead_adder_subtractor_1_s7, carry_lookahead_adder_subtractor_1_s8,
       carry_lookahead_adder_subtractor_1_s9, carry_lookahead_adder_subtractor_1_s10,
       carry_lookahead_adder_subtractor_1_s11, carry_lookahead_adder_subtractor_1_s12,
       carry_lookahead_adder_subtractor_1_s13, carry_lookahead_adder_subtractor_1_s14,
       carry_lookahead_adder_subtractor_1_s15, controlled_buffer_2_out, Flip_A_B, four_bit_left_shift_1_z2,
       four_bit_left_shift_1_z3, four_bit_left_shift_1_z4, four_bit_left_shift_1_z5,
       four_bit_left_shift_1_z6, four_bit_left_shift_1_z7, four_bit_left_shift_1_z8,
       four_bit_left_shift_1_z9, four_bit_left_shift_1_z10, four_bit_left_shift_1_z11,
       four_bit_left_shift_1_z12, four_bit_left_shift_1_z13, four_bit_left_shift_1_z14,
       four_bit_left_shift_1_z15, four_bit_right_shift_1_z2, four_bit_right_shift_1_z3,
       four_bit_right_shift_1_z4, four_bit_right_shift_1_z5, four_bit_right_shift_1_z6,
       four_bit_right_shift_1_z7, four_bit_right_shift_1_z8, four_bit_right_shift_1_z9,
       four_bit_right_shift_1_z10, four_bit_right_shift_1_z11, four_bit_right_shift_1_z12,
       four_bit_right_shift_1_z13, four_bit_right_shift_1_z14, four_bit_right_shift_1_z15, IR_Shift_0_CS_t,
       one_bit_left_shift_1_z2, one_bit_left_shift_1_z3, one_bit_left_shift_1_z4, one_bit_left_shift_1_z5,
       one_bit_left_shift_1_z6, one_bit_left_shift_1_z7, one_bit_left_shift_1_z8, one_bit_left_shift_1_z9,
       one_bit_left_shift_1_z10, one_bit_left_shift_1_z11, one_bit_left_shift_1_z12,
       one_bit_left_shift_1_z13, one_bit_left_shift_1_z14, one_bit_left_shift_1_z15, or_4_out, or_5_out,
       undriven, undriven_2, undriven_3, undriven_4, undriven_5, undriven_6, undriven_7, undriven_8,
       undriven_9, undriven_10, undriven_11, undriven_12, undriven_14, undriven_15, undriven_16, undriven_17,
       undriven_18, undriven_19, undriven_20, undriven_21, undriven_22, undriven_23, undriven_24,
       undriven_25, undriven_26, undriven_27, undriven_28, undriven_29, undriven_30, undriven_31,
       undriven_32, undriven_33, undriven_34, undriven_35, undriven_36, undriven_37, undriven_38,
       undriven_39, undriven_40, undriven_41, undriven_42, undriven_43, undriven_44, undriven_45,
       undriven_46, undriven_47, undriven_48, undriven_49, undriven_50, undriven_51, undriven_52,
       undriven_53, undriven_54, undriven_55, undriven_56, undriven_57, undriven_58, undriven_59,
       undriven_60, undriven_61, undriven_62, undriven_63, undriven_64, undriven_65, undriven_66,
       undriven_67, undriven_68, undriven_69, undriven_70, undriven_71;
  wire [1:0] buffer_1_out, carry_lookahead_adder_subtractor_1_s0, controlled_buffer_1_out,
       controlled_buffer_3_out, controlled_buffer_4_out, controlled_buffer_5_out, controlled_buffer_6_out,
       controlled_buffer_7_out, controlled_buffer_8_out, four_bit_right_shift_1_z0, multiplexer_1_out,
       multiplexer_2_out, multiplexer_3_out, one_bit_left_shift_1_z0, or_1_out, or_2_out;
  wire [1:1] multiplexer_4_out, undriven_13;

  Multiplexer #(.enable("false"), .width(2)) multiplexer_1 (
    .in0(multiplexer_2_out), .in1({undriven_13[1], Y_In}), .out(multiplexer_1_out), .sel(Flip_A_B));
  assign controlled_buffer_1_out[0] = Bus_In_CS ? Bus_In : 1'bz;  // Controlled_Buffer controlled_buffer_1
  One_Bit_Left_Shift one_bit_left_shift_1 (
    .Z3(one_bit_left_shift_1_z3), .Z2(one_bit_left_shift_1_z2), .Z1(one_bit_left_shift_1_z0[1]),
    .Z0(one_bit_left_shift_1_z0[0]), .Z15(one_bit_left_shift_1_z15), .Z14(one_bit_left_shift_1_z14),
    .Z13(one_bit_left_shift_1_z13), .Z12(one_bit_left_shift_1_z12), .Z11(one_bit_left_shift_1_z11),
    .Z10(one_bit_left_shift_1_z10), .Z9(one_bit_left_shift_1_z9), .Z8(one_bit_left_shift_1_z8),
    .Z7(one_bit_left_shift_1_z7), .Z6(one_bit_left_shift_1_z6), .Z5(one_bit_left_shift_1_z5),
    .Z4(one_bit_left_shift_1_z4), .A3(undriven_30), .A2(undriven_32), .A1(controlled_buffer_1_out[1]),
    .A0(controlled_buffer_1_out[0]), .S0(controlled_buffer_2_out), .A15(undriven_8), .A14(undriven_10),
    .A13(undriven_12), .A12(undriven_15), .A11(undriven_17), .A10(undriven_19), .A9(undriven_21),
    .A8(undriven_23), .A7(undriven_24), .A6(undriven_25), .A5(undriven_26), .A4(undriven_28));
  Multiplexer #(.enable("false"), .width(2)) multiplexer_2 (
    .in0(one_bit_left_shift_1_z0), .in1(2'b10), .out(multiplexer_2_out), .sel(ALU_Inc_2));
  Carry_Lookahead_Adder_Subtractor carry_lookahead_adder_subtractor_1 (
    .S13(carry_lookahead_adder_subtractor_1_s13), .S12(carry_lookahead_adder_subtractor_1_s12),
    .S11(carry_lookahead_adder_subtractor_1_s11), .S10(carry_lookahead_adder_subtractor_1_s10),
    .S9(carry_lookahead_adder_subtractor_1_s9), .S8(carry_lookahead_adder_subtractor_1_s8),
    .S7(carry_lookahead_adder_subtractor_1_s7), .S6(carry_lookahead_adder_subtractor_1_s6),
    .S5(carry_lookahead_adder_subtractor_1_s5), .S4(carry_lookahead_adder_subtractor_1_s4),
    .S3(carry_lookahead_adder_subtractor_1_s3), .S2(carry_lookahead_adder_subtractor_1_s2),
    .S1(carry_lookahead_adder_subtractor_1_s0[1]), .S0(carry_lookahead_adder_subtractor_1_s0[0]),
    .S15(carry_lookahead_adder_subtractor_1_s15), .S14(carry_lookahead_adder_subtractor_1_s14),
    .A12(undriven_4), .B12(undriven_33), .A11(undriven_5), .B11(undriven_34), .A10(undriven_6),
    .B10(undriven_35), .A9(undriven_7), .B9(undriven_36), .A8(undriven_9), .B8(undriven_37),
    .A7(undriven_11), .B7(undriven_38), .A6(undriven_14), .B6(undriven_39), .A5(undriven_16),
    .B5(undriven_40), .A4(undriven_18), .B4(undriven_41), .A3(undriven_20), .B3(undriven_42),
    .A2(undriven_22), .B2(undriven_43), .A1(multiplexer_1_out[1]), .B1(multiplexer_3_out[1]),
    .A0(multiplexer_1_out[0]), .B0(multiplexer_3_out[0]), .Mode(ALU_SUB), .A15(undriven), .B15(undriven_27),
    .A14(undriven_2), .B14(undriven_29), .A13(undriven_3), .B13(undriven_31));
  and and_1 (Flip_A_B, ALU_SUB, IR_Shift_0_CS_t);
  assign controlled_buffer_2_out = IR_Shift_0_CS ? IR_Shift : 1'bz;  // Controlled_Buffer controlled_buffer_2
  Multiplexer #(.enable("false"), .width(2)) multiplexer_3 (
    .in0({undriven_13[1], Y_In}), .in1(multiplexer_2_out), .out(multiplexer_3_out), .sel(Flip_A_B));
  assign controlled_buffer_3_out = ALU_OR ? {undriven_13[1], Y_In} : 2'bz;  // Controlled_Buffer controlled_buffer_3
  assign controlled_buffer_4_out = ALU_OR ? controlled_buffer_1_out : 2'bz;  // Controlled_Buffer controlled_buffer_4
  assign or_1_out = controlled_buffer_3_out | controlled_buffer_4_out;  // OR_Gate or_1, 2 bits wide
  assign controlled_buffer_5_out = ALU_AND ? controlled_buffer_1_out : 2'bz;  // Controlled_Buffer controlled_buffer_5
  assign controlled_buffer_6_out = ALU_AND ? {undriven_13[1], Y_In} : 2'bz;  // Controlled_Buffer controlled_buffer_6
  assign buffer_1_out = controlled_buffer_1_out;  // Buffer buffer_1, 2 bits wide
  assign or_1_out = controlled_buffer_5_out & controlled_buffer_6_out;  // AND_Gate and_2, 2 bits wide
  assign buffer_1_out = ALU_NOT ? ~controlled_buffer_1_out : 2'bz;  // Controlled_Inverter controlled_inverter_1
  Multiplexer #(.enable("false"), .select(2), .width(2)) multiplexer_4 (
    .in0(carry_lookahead_adder_subtractor_1_s0), .in1(or_1_out), .in2(buffer_1_out),
    .in3(four_bit_right_shift_1_z0), .out({multiplexer_4_out[1], Z_Out}), .sel(or_2_out));
  assign controlled_buffer_7_out = ALU_RS ? {undriven_13[1], Y_In} : 2'bz;  // Controlled_Buffer controlled_buffer_7
  Four_Bit_Right_Shift four_bit_right_shift_1 (
    .Z3(four_bit_right_shift_1_z3), .Z2(four_bit_right_shift_1_z2), .Z1(four_bit_right_shift_1_z0[1]),
    .Z0(four_bit_right_shift_1_z0[0]), .Z15(four_bit_right_shift_1_z15), .Z14(four_bit_right_shift_1_z14),
    .Z13(four_bit_right_shift_1_z13), .Z12(four_bit_right_shift_1_z12), .Z11(four_bit_right_shift_1_z11),
    .Z10(four_bit_right_shift_1_z10), .Z9(four_bit_right_shift_1_z9), .Z8(four_bit_right_shift_1_z8),
    .Z7(four_bit_right_shift_1_z7), .Z6(four_bit_right_shift_1_z6), .Z5(four_bit_right_shift_1_z5),
    .Z4(four_bit_right_shift_1_z4), .A3(undriven_56), .A2(undriven_57), .A1(controlled_buffer_7_out[1]),
    .A0(controlled_buffer_7_out[0]), .S0(S0), .S1(S1), .S2(S2), .S3(S3), .A15(undriven_44),
    .A14(undriven_45), .A13(undriven_46), .A12(undriven_47), .A11(undriven_48), .A10(undriven_49),
    .A9(undriven_50), .A8(undriven_51), .A7(undriven_52), .A6(undriven_53), .A5(undriven_54), .A4(undriven_55));
  or or_2 (or_2_out[0], ALU_ADD, ALU_SUB);
  or or_3 (or_2_out[1], ALU_OR, ALU_AND);
  or or_4 (or_4_out, ALU_PASS, ALU_NOT);
  or or_5 (or_5_out, ALU_RS, ALU_LS);
  assign controlled_buffer_8_out = ALU_LS ? {undriven_13[1], Y_In} : 2'bz;  // Controlled_Buffer controlled_buffer_8
  Four_Bit_Left_Shift four_bit_left_shift_1 (
    .Z4(four_bit_left_shift_1_z4), .Z3(four_bit_left_shift_1_z3), .Z2(four_bit_left_shift_1_z2),
    .Z1(four_bit_right_shift_1_z0[1]), .Z0(four_bit_right_shift_1_z0[0]), .Z15(four_bit_left_shift_1_z15),
    .Z14(four_bit_left_shift_1_z14), .Z13(four_bit_left_shift_1_z13), .Z12(four_bit_left_shift_1_z12),
    .Z11(four_bit_left_shift_1_z11), .Z10(four_bit_left_shift_1_z10), .Z9(four_bit_left_shift_1_z9),
    .Z8(four_bit_left_shift_1_z8), .Z7(four_bit_left_shift_1_z7), .Z6(four_bit_left_shift_1_z6),
    .Z5(four_bit_left_shift_1_z5), .A3(undriven_70), .A2(undriven_71), .A1(controlled_buffer_8_out[1]),
    .A0(controlled_buffer_8_out[0]), .S0(S0), .S1(S1), .S2(S2), .S3(S3), .A15(undriven_58),
    .A14(undriven_59), .A13(undriven_60), .A12(undriven_61), .A11(undriven_62), .A10(undriven_63),
    .A9(undriven_64), .A8(undriven_65), .A7(undriven_66), .A6(undriven_67), .A5(undriven_68), .A4(undriven_69));
  assign {ALU_OR, ALU_RS, ALU_LS, ALU_AND, ALU_SUB, ALU_ADD} = ALU_Opcode_Task ? {OP5, OP4, OP3, OP2, OP1, OP0} : 6'bz;  // Controlled_Buffer controlled_buffer_9
endmodule

module Y_Register (
  input  Y_In,
  input  Y_In_CS,
  input  Clock,
  input  Reset,
  input  Y_Out_CS,
  output S0,
  output S1,
  output S2,
  output S3,
  output Y_Out
);

  wire controlled_buffer_1_out, sixteen_bit_register_1_q4, sixteen_bit_register_1_q5,
       sixteen_bit_register_1_q6, sixteen_bit_register_1_q7, sixteen_bit_register_1_q8,
       sixteen_bit_register_1_q9, sixteen_bit_register_1_q10, sixteen_bit_register_1_q11,
       sixteen_bit_register_1_q12, sixteen_bit_register_1_q13, sixteen_bit_register_1_q14,
       sixteen_bit_register_1_q15, undriven, undriven_2, undriven_3, undriven_4, undriven_5, undriven_6,
       undriven_7, undriven_8, undriven_9, undriven_10, undriven_11, undriven_12, undriven_13, undriven_14,
       undriven_15;

  assign controlled_buffer_1_out = Y_In_CS ? Y_In : 1'bz;  // Controlled_Buffer controlled_buffer_1
  Sixteen_Bit_Register sixteen_bit_register_1 (
    .Q4(sixteen_bit_register_1_q4), .Q8(sixteen_bit_register_1_q8), .Q12(sixteen_bit_register_1_q12),
    .Q0(S0), .Q5(sixteen_bit_register_1_q5), .Q9(sixteen_bit_register_1_q9),
    .Q13(sixteen_bit_register_1_q13), .Q1(S1), .Q6(sixteen_bit_register_1_q6),
    .Q10(sixteen_bit_register_1_q10), .Q14(sixteen_bit_register_1_q14), .Q2(S2),
    .Q7(sixteen_bit_register_1_q7), .Q11(sixteen_bit_register_1_q11), .Q15(sixteen_bit_register_1_q15),
    .Q3(S3), .Clock(Clock), .Reset(Reset), .D0(controlled_buffer_1_out), .D4(undriven_12), .D8(undriven_8),
    .D12(undriven_4), .D1(undriven_15), .D5(undriven_11), .D9(undriven_7), .D13(undriven_3),
    .D2(undriven_14), .D6(undriven_10), .D10(undriven_6), .D14(undriven_2), .D3(undriven_13),
    .D7(undriven_9), .D11(undriven_5), .D15(undriven));
  assign Y_Out = Y_Out_CS ? S0 : 1'bz;  // Controlled_Buffer controlled_buffer_2
endmodule

module Z_Register (
  input  Z_In,
  input  Z_In_CS,
  input  Clock,
  input  Reset,
  input  Z_Out_CS,
  input  SET_CC,
  output Z_Out,
  output PSW_Z,
  output PSW_N
);

  wire controlled_buffer_1_out, nor_1_out, sixteen_bit_register_1_q0, sixteen_bit_register_1_q1,
       sixteen_bit_register_1_q2, sixteen_bit_register_1_q3, sixteen_bit_register_1_q4,
       sixteen_bit_register_1_q5, sixteen_bit_register_1_q6, sixteen_bit_register_1_q7,
       sixteen_bit_register_1_q8, sixteen_bit_register_1_q9, sixteen_bit_register_1_q10,
       sixteen_bit_register_1_q11, sixteen_bit_register_1_q12, sixteen_bit_register_1_q13,
       sixteen_bit_register_1_q14, sixteen_bit_register_1_q15, undriven, undriven_2, undriven_3, undriven_4,
       undriven_5, undriven_6, undriven_7, undriven_8, undriven_9, undriven_10, undriven_11, undriven_12,
       undriven_13, undriven_14, undriven_15;

  assign controlled_buffer_1_out = Z_In_CS ? Z_In : 1'bz;  // Controlled_Buffer controlled_buffer_1
  Sixteen_Bit_Register sixteen_bit_register_1 (
    .Q4(sixteen_bit_register_1_q4), .Q8(sixteen_bit_register_1_q8), .Q12(sixteen_bit_register_1_q12),
    .Q0(sixteen_bit_register_1_q0), .Q5(sixteen_bit_register_1_q5), .Q9(sixteen_bit_register_1_q9),
    .Q13(sixteen_bit_register_1_q13), .Q1(sixteen_bit_register_1_q1), .Q6(sixteen_bit_register_1_q6),
    .Q10(sixteen_bit_register_1_q10), .Q14(sixteen_bit_register_1_q14), .Q2(sixteen_bit_register_1_q2),
    .Q7(sixteen_bit_register_1_q7), .Q11(sixteen_bit_register_1_q11), .Q15(sixteen_bit_register_1_q15),
    .Q3(sixteen_bit_register_1_q3), .Clock(Clock), .Reset(Reset), .D0(controlled_buffer_1_out),
    .D4(undriven_12), .D8(undriven_8), .D12(undriven_4), .D1(undriven_15), .D5(undriven_11), .D9(undriven_7),
    .D13(undriven_3), .D2(undriven_14), .D6(undriven_10), .D10(undriven_6), .D14(undriven_2),
    .D3(undriven_13), .D7(undriven_9), .D11(undriven_5), .D15(undriven));
  nor nor_1 (nor_1_out, sixteen_bit_register_1_q15, sixteen_bit_register_1_q14, sixteen_bit_register_1_q13, sixteen_bit_register_1_q12, sixteen_bit_register_1_q11, sixteen_bit_register_1_q10, sixteen_bit_register_1_q9, sixteen_bit_register_1_q8, sixteen_bit_register_1_q7, sixteen_bit_register_1_q6, sixteen_bit_register_1_q5, sixteen_bit_register_1_q4, sixteen_bit_register_1_q3, sixteen_bit_register_1_q2, sixteen_bit_register_1_q1, sixteen_bit_register_1_q0);
  assign Z_Out = Z_Out_CS ? sixteen_bit_register_1_q0 : 1'bz;  // Controlled_Buffer controlled_buffer_2
  assign PSW_Z = SET_CC ? nor_1_out : 1'bz;  // Controlled_Buffer controlled_buffer_3
  assign PSW_N = SET_CC ? sixteen_bit_register_1_q15 : 1'bz;  // Controlled_Buffer controlled_buffer_4
endmodule
