// Logisim project project-3-control-unit.circ as structural Verilog: 4 circuits, main circuit State_Decoder
module State_Decoder (
  input  Clock,
  input  [4:0] Next_State,
  output [28:0] Current_State_One_Hot
);

  wire decoder_1_out0, decoder_1_out1, decoder_1_out2;
  wire [4:0] d_ff_5_qn;

  D_Flip_Flop d_ff_1 (.clk(Clock), .D(Next_State[4]), .Qn(d_ff_5_qn[4]));  // open: Q, preset, reset
  D_Flip_Flop d_ff_2 (.clk(Clock), .D(Next_State[3]), .Qn(d_ff_5_qn[3]));  // open: Q, preset, reset
  D_Flip_Flop d_ff_3 (.clk(Clock), .D(Next_State[2]), .Qn(d_ff_5_qn[2]));  // open: Q, preset, reset
  D_Flip_Flop d_ff_4 (.clk(Clock), .D(Next_State[1]), .Qn(d_ff_5_qn[1]));  // open: Q, preset, reset
  D_Flip_Flop d_ff_5 (.clk(Clock), .D(Next_State[0]), .Qn(d_ff_5_qn[0]));  // open: Q, preset, reset
  Decoder #(.enable("false"), .select(5)) decoder_1 (
    .out0(decoder_1_out0), .out1(decoder_1_out1), .out2(decoder_1_out2), .out3(Current_State_One_Hot[28]),
    .out4(Current_State_One_Hot[27]), .out5(Current_State_One_Hot[26]), .out6(Current_State_One_Hot[25]),
    .out7(Current_State_One_Hot[24]), .out8(Current_State_One_Hot[23]), .out9(Current_State_One_Hot[22]),
    .out10(Current_State_One_Hot[21]), .out11(Current_State_One_Hot[20]), .out12(Current_State_One_Hot[19]),
    .out13(Current_State_One_Hot[18]), .out14(Current_State_One_Hot[17]), .out15(Current_State_One_Hot[16]),
    .out16(Current_State_One_Hot[15]), .out17(Current_State_One_Hot[14]), .out18(Current_State_One_Hot[13]),
    .out19(Current_State_One_Hot[12]), .out20(Current_State_One_Hot[11]), .out21(Current_State_One_Hot[10]),
    .out22(Current_State_One_Hot[9]), .out23(Current_State_One_Hot[8]), .out24(Current_State_One_Hot[7]),
    .out25(Current_State_One_Hot[6]), .out26(Current_State_One_Hot[5]), .out27(Current_State_One_Hot[4]),
    .out28(Current_State_One_Hot[3]), .out29(Current_State_One_Hot[2]), .out30(Current_State_One_Hot[1]),
    .out31(Current_State_One_Hot[0]), .sel(d_ff_5_qn));
  // NoConnect on decoder_1_out0
  // NoConnect on decoder_1_out1
  // NoConnect on decoder_1_out2
endmodule

module State_Controller (
  input  [28:0] Current_State,
  output Reset,
  output IR_In_CS,
  output IR_Short_Off_CS,
  output IR_Long_Off_CS,
  output PC_In,
  output PC_Out,
  output GPR_Rd_In,
  output GPR_Rd_Out,
  output GPR_Rs2_Out,
  output GPR_Rs1_Out,
  output GPR_0_Out_CS,
  output MAR_Bus_In_CS,
  output MDR_Bus_Out_CS,
  output MDR_Bus_In_CS,
  output READ_MM,
  output WRITE_MM,
  output ALU_In_Right,
  output ALU_In_Left,
  output ALU_Opcode_Task,
  output ALU_Leftshift_IR_shift,
  output ALU_NOT,
  output ALU_ADD,
  output ALU_Inc_2,
  output Z_In,
  output Z_Out,
  output Y_In,
  output ROM_Out_CS,
  output Timer_In,
  output PSW_In,
  output PSW_Out
);

  or or_1 (PC_In, Current_State[2], Current_State[11], Current_State[28]);
  or or_2 (PC_Out, Current_State[1], Current_State[24], Current_State[16]);
  or or_3 (GPR_Rd_In, Current_State[7], Current_State[13], Current_State[16]);
  or or_4 (GPR_Rd_Out, Current_State[14], Current_State[17]);
  or or_5 (MAR_Bus_In_CS, Current_State[1], Current_State[9], Current_State[15], Current_State[20], Current_State[21], Current_State[23], Current_State[25], Current_State[27]);
  or or_6 (MDR_Bus_Out_CS, Current_State[3], Current_State[12], Current_State[13], Current_State[18], Current_State[19], Current_State[26], Current_State[28]);
  or or_7 (MDR_Bus_In_CS, Current_State[14], Current_State[22], Current_State[24]);
  or or_8 (READ_MM, Current_State[1], Current_State[9], Current_State[25], Current_State[27]);
  or or_9 (WRITE_MM, Current_State[15], Current_State[22], Current_State[24]);
  or or_10 (ALU_In_Right, Current_State[4], Current_State[6], Current_State[8], Current_State[10], Current_State[12]);
  or or_11 (ALU_In_Left, Current_State[6], Current_State[8], Current_State[10]);
  or or_12 (ALU_ADD, Current_State[8], Current_State[10]);
  or or_13 (ALU_Inc_2, Current_State[1], Current_State[22], Current_State[24], Current_State[26]);
  or or_14 (Z_In, Current_State[1], Current_State[4], Current_State[6], Current_State[8], Current_State[10], Current_State[12], Current_State[22], Current_State[24], Current_State[26]);
  or or_15 (Z_Out, Current_State[2], Current_State[5], Current_State[7], Current_State[9], Current_State[11], Current_State[15], Current_State[23], Current_State[25], Current_State[27]);
  or or_16 (Y_In, Current_State[2], Current_State[5], Current_State[17], Current_State[20], Current_State[21], Current_State[23], Current_State[25]);
  or or_17 (PSW_In, Current_State[19], Current_State[26]);

  assign ALU_Leftshift_IR_shift = Current_State[4];
  assign ALU_NOT = Current_State[12];
  assign ALU_Opcode_Task = Current_State[6];
  assign GPR_0_Out_CS = Current_State[20];
  assign GPR_Rs1_Out = Current_State[6];
  assign GPR_Rs2_Out = Current_State[4];
  assign IR_In_CS = Current_State[3];
  assign IR_Long_Off_CS = Current_State[10];
  assign IR_Short_Off_CS = Current_State[8];
  assign PSW_Out = Current_State[22];
  assign Reset = Current_State[0];
  assign ROM_Out_CS = Current_State[21];
  assign Timer_In = Current_State[18];
endmodule

module State_Switcher (
  input  [28:0] Current_State,
  input  [15:0] Opcode,
  input  PSW_Z,
  input  PSW_N,
  input  PSW_P,
  input  Timer_Flag,
  output [4:0] Next_State
);

  wire and_1_out, and_2_out, and_3_out, and_4_out, and_5_out, and_6_out, and_7_out, and_8_out, and_9_out,
       and_10_out, and_11_out, and_12_out, and_13_out, and_14_out, and_15_out, and_16_out, and_17_out,
       and_18_out, and_19_out, and_20_out, and_21_out, and_22_out, next_cycle, not_1_out, not_2_out,
       not_3_out, not_4_out, or_1_out, or_2_out, or_3_out, or_4_out, or_5_out, or_6_out, or_7_out, or_8_out,
       or_9_out, or_10_out, or_11_out, or_12_out;

  not not_1 (not_1_out, Timer_Flag);
  or or_1 (or_1_out, Opcode[0], Opcode[1], Opcode[2], Opcode[3], Opcode[4], Opcode[5]);
  or or_2 (or_2_out, Current_State[6], Current_State[12]);
  or or_3 (or_3_out, Opcode[6], Opcode[7], Opcode[8]);
  or or_4 (or_4_out, Opcode[6], Opcode[7]);
  or or_5 (or_5_out, Opcode[14], Opcode[15]);
  and and_1 (and_1_out, PSW_N, Opcode[9]);
  and and_2 (and_2_out, PSW_Z, Opcode[10]);
  or or_6 (or_6_out, Opcode[9], Opcode[10], Opcode[11]);
  and and_3 (and_3_out, Current_State[8], Opcode[12]);
  and and_4 (and_4_out, Current_State[9], Opcode[6]);
  and and_5 (and_5_out, Current_State[9], Opcode[7]);
  and and_6 (and_6_out, Current_State[8], Opcode[8]);
  and and_7 (and_7_out, Current_State[3], Opcode[12]);
  and and_8 (and_8_out, Current_State[3], Opcode[13]);
  and and_9 (and_9_out, Current_State[9], Opcode[14]);
  and and_10 (and_10_out, Current_State[9], Opcode[15]);
  or or_7 (or_7_out, Opcode[14], Opcode[15]);
  not not_2 (not_2_out, PSW_P);
  or or_8 (or_8_out, Current_State[20], Current_State[21]);
  and and_11 (and_11_out, Current_State[8], Opcode[13]);
  not not_3 (not_3_out, PSW_N);
  not not_4 (not_4_out, PSW_Z);
  and and_12 (and_12_out, not_1_out, next_cycle);
  and and_13 (and_13_out, Current_State[3], or_1_out);
  and and_14 (and_14_out, or_3_out, Current_State[3]);
  and and_15 (and_15_out, or_4_out, Current_State[8]);
  and and_16 (and_16_out, or_5_out, Current_State[10]);
  or or_9 (or_9_out, and_1_out, and_2_out, Opcode[11], Opcode[14], Opcode[15]);
  and and_17 (and_17_out, or_6_out, Current_State[10]);
  and and_18 (and_18_out, or_7_out, Current_State[3], not_2_out);
  and and_19 (and_19_out, Timer_Flag, next_cycle);
  and and_20 (and_20_out, Current_State[3], Opcode[9], not_3_out);
  and and_21 (and_21_out, Current_State[3], Opcode[10], not_4_out);
  or or_10 (or_10_out, and_14_out, Current_State[16], Current_State[17]);
  or or_11 (or_11_out, and_15_out, and_16_out);
  and and_22 (and_22_out, or_9_out, Current_State[3]);
  or or_12 (or_12_out, and_17_out, and_3_out);
  or or_13 (next_cycle, Current_State[0], Current_State[7], Current_State[11], Current_State[15], Current_State[18], Current_State[19], Current_State[28], and_11_out, and_20_out, and_21_out);
  Priority_Encoder #(.select(5)) priority_encoder_1 (
    .in0(1'b0), .in1(and_12_out), .in2(Current_State[1]), .in3(Current_State[2]), .in4(and_13_out),
    .in5(Current_State[4]), .in6(Current_State[5]), .in7(or_2_out), .in8(or_10_out), .in9(or_11_out),
    .in10(and_22_out), .in11(or_12_out), .in12(and_4_out), .in13(and_5_out), .in14(and_6_out),
    .in15(Current_State[14]), .in16(and_7_out), .in17(and_8_out), .in18(and_9_out), .in19(and_10_out),
    .in20(and_18_out), .in21(and_19_out), .in22(or_8_out), .in23(Current_State[22]),
    .in24(Current_State[23]), .in25(Current_State[25]), .in26(Current_State[26]), .in27(Current_State[27]),
    .in28(1'b0), .in29(1'b0), .in30(1'b0), .out(Next_State), .en_in(1'b1));  // open: in31, gs, en_out

  assign Current_State[24] = Current_State[25];
endmodule

module Control_Unit (
  input  PSW_Z,
  input  PSW_N,
  input  PSW_P,
  input  Timer_Flag,
  input  [15:0] Opcode,
  input  Clock,
  output Reset,
  output IR_In_CS,
  output IR_Short_Off_CS,
  output IR_Long_Off_CS,
  output PC_In,
  output PC_Out,
  output GPR_Rd_In,
  output GPR_Rd_Out,
  output GPR_Rs2_Out,
  output GPR_Rs1_Out,
  output GPR_0_Out_CS,
  output MAR_Bus_In_CS,
  output MDR_Bus_Out_CS,
  output MDR_Bus_In_CS,
  output READ_MM,
  output WRITE_MM,
  output ALU_In_Right,
  output ALU_In_Left,
  output ALU_Opcode_Task,
  output ALU_Leftshift_IR_Shift,
  output ALU_NOT,
  output ALU_ADD,
  output ALU_Inc_2,
  output Z_In_CS,
  output Z_Out_CS,
  output Y_In_CS,
  output ROM_Out_CS,
  output Timer_In,
  output PSW_In_CS,
  output PSW_Out_CS
);

  wire [4:0] state_switcher_1_next_state;
  wire [28:0] undriven;

  State_Decoder state_decoder_1 (
    .Clock(Clock), .Next_State(state_switcher_1_next_state));  // open: Current_State_One_Hot
  State_Switcher state_switcher_1 (
    .Next_State(state_switcher_1_next_state), .PSW_Z(PSW_Z), .PSW_N(PSW_N), .PSW_P(PSW_P),
    .Timer_Flag(Timer_Flag), .Current_State(undriven), .Opcode(Opcode));
  State_Controller state_controller_1 (
    .Z_In(Z_In_CS), .Z_Out(Z_Out_CS), .Y_In(Y_In_CS), .Reset(Reset), .ROM_Out_CS(ROM_Out_CS),
    .Timer_In(Timer_In), .PSW_In(PSW_In_CS), .PSW_Out(PSW_Out_CS), .IR_In_CS(IR_In_CS),
    .IR_Short_Off_CS(IR_Short_Off_CS), .IR_Long_Off_CS(IR_Long_Off_CS), .PC_In(PC_In), .PC_Out(PC_Out),
    .GPR_Rd_In(GPR_Rd_In), .GPR_Rd_Out(GPR_Rd_Out), .GPR_Rs2_Out(GPR_Rs2_Out), .GPR_Rs1_Out(GPR_Rs1_Out),
    .GPR_0_Out_CS(GPR_0_Out_CS), .MAR_Bus_In_CS(MAR_Bus_In_CS), .MDR_Bus_Out_CS(MDR_Bus_Out_CS),
    .MDR_Bus_In_CS(MDR_Bus_In_CS), .READ_MM(READ_MM), .WRITE_MM(WRITE_MM), .ALU_In_Right(ALU_In_Right),
    .ALU_In_Left(ALU_In_Left), .ALU_Opcode_Task(ALU_Opcode_Task),
    .ALU_Leftshift_IR_shift(ALU_Leftshift_IR_Shift), .ALU_NOT(ALU_NOT), .ALU_ADD(ALU_ADD),
    .ALU_Inc_2(ALU_Inc_2), .Current_State(undriven));
endmodule
